// Logisim project BasicLogicGates_Adders.circ as structural Verilog: 25 circuits, main circuit main
module main (
  input  I0,
  input  A,
  input  I1,
  input  S_prime,
  input  B,
  input  S0,
  input  A_2,
  input  R_prime,
  input  I0_2,
  input  B_2,
  input  S,
  input  I1_2,
  input  A_3,
  input  I2,
  input  I3,
  input  EN,
  input  B_3,
  input  R,
  input  S0_2,
  input  Cin,
  input  S1,
  input  D,
  input  I0_3,
  input  EN_2,
  input  O0,
  input  A3,
  input  LOGIC1,
  input  PRE_prime,
  input  B3,
  input  D_2,
  input  I0_4,
  input  A1,
  input  Clk,
  input  A0,
  input  S0_3,
  input  B1,
  input  CLR_prime,
  input  B0,
  input  S1_2,
  input  A2,
  input  PRE_prime_2,
  input  Cin_2,
  input  B2,
  input  T,
  input  Clk_2,
  input  I3_2,
  input  CLR_prime_2,
  input  I2_2,
  input  I1_3,
  input  A1_2,
  input  PRE_prime_3,
  input  I0_5,
  input  A3_2,
  input  A2_2,
  input  B1_2,
  input  J,
  input  B3_2,
  input  K,
  input  B2_2,
  input  Clk_3,
  input  CLR_prime_3,
  input  A0_2,
  input  I0_6,
  input  B0_2,
  input  I1_4,
  input  PRE_prime_4,
  input  DATA,
  input  LOAD,
  input  Clk_4,
  input  CLR_prime_4,
  input  LOGIC1_2,
  input  PRE_prime_5,
  input  Clk_5,
  input  PRE_prime_6,
  input  CLR_prime_5,
  input  CLR_prime_6,
  input  Clk_6,
  input  LOAD_2,
  input  D0,
  input  D1,
  input  D2,
  input  D3,
  input  PRE_prime_7,
  input  CLR_prime_7,
  input  Clk_7,
  input  EN_3,
  input  LOAD_3,
  input  D0_2,
  input  D1_2,
  input  D2_2,
  input  D3_2,
  input  PRE_prime_8,
  input  I,
  input  Clk_8,
  input  SHIFT,
  input  CLR_prime_8,
  input  DIR_1______0,
  input  Lin,
  input  Rin,
  input  PRE_prime_9,
  input  SHIFT_2,
  input  Clk_9,
  input  CLR_prime_9,
  input  P3,
  input  P2,
  input  P1,
  input  P0,
  input  DIR_1______0_2,
  input  Lin_2,
  input  Rin_2,
  input  PRE_prime_10,
  input  INPUT_MODE_1_ParallelIn__0_SerialIn,
  input  SHIFT_3,
  input  Clk_10,
  input  CLR_prime_10,
  input  OUTPUT_MODE_Parallel_1__Serial_0,
  output S_2,
  output Output,
  output Q,
  output L_A_B,
  output C,
  output Q_prime,
  output E,
  output Q_2,
  output Output_2,
  output G_A_B,
  output Q_prime_2,
  output S_3,
  output Q_3,
  output C_2,
  output Q_prime_3,
  output O0_2,
  output L_A_B_2,
  output O1,
  output Q_4,
  output O0_3,
  output Q_prime_4,
  output O1_2,
  output O2,
  output S1_3,
  output S0_4,
  output O3,
  output Q_5,
  output Q_prime_5,
  output O0_4,
  output E_2,
  output O1_3,
  output Q_6,
  output Valid,
  output Q_prime_6,
  output S3,
  output S2,
  output Cout,
  output O0_5,
  output O1_4,
  output O2_2,
  output O3_2,
  output O,
  output G_A_B_2,
  output O_2,
  output O_3,
  output O_4,
  output O_5,
  output O_6,
  output O_7,
  output O_8,
  output O_9,
  output O_10,
  output O_11,
  output O_12,
  output O_13,
  output O_14,
  output Lout,
  output Rout,
  output Lout_2,
  output Rout_2,
  output O3_3,
  output O2_3,
  output O1_5,
  output O0_6
);

  wire dflipflop_1_q, dflipflop_12_q, dflipflop_13_q, dflipflop_14_q, dflipflop_15_q, dflipflop_17_q,
       dflipflop_18_q, dflipflop_20_q, dflipflop_21_q, n2_1mux_1_output, n2_1mux_2_output, n2_1mux_3_output,
       n2_1mux_4_output, n2_1mux_5_output, n2_1mux_6_output, n2_1mux_7_output, n2_1mux_8_output,
       n2_1mux_9_output, n2_1mux_10_output, n2_1mux_11_output, n2_1mux_12_output, n2_1mux_13_output,
       n2_1mux_14_output, n2_1mux_15_output, n2_1mux_16_output, n2_1mux_17_output, n2_1mux_18_output,
       n2_1mux_19_output, n2_1mux_20_output, n2_1mux_21_output, n2_1mux_22_output, n2_1mux_24_output,
       n2_1mux_25_output, nand_1_out, nand_2_out, nand_3_out, nand_4_out, nand_5_out, nand_6_out, nand_7_out,
       nand_8_out, nand_9_out, nand_10_out, nand_11_out, nand_12_out, nand_13_out, nand_14_out, nand_15_out,
       nand_16_out, nand_17_out, nand_18_out, nand_19_out, nand_20_out, nand_21_out, nand_22_out,
       nand_23_out, nand_24_out, nand_25_out, nand_26_out, nand_27_out, nand_28_out, nand_29_out,
       nand_30_out, nand_31_out, nand_32_out, nand_33_out, nand_34_out, nand_35_out, nand_36_out,
       nand_37_out, nand_38_out, nand_39_out, nand_41_out, nand_43_out, nand_44_out, nand_45_out,
       nand_46_out, nand_47_out, nand_48_out, nand_49_out, nand_50_out, nand_52_out, nand_53_out,
       nand_54_out, nand_55_out, nand_56_out, nand_57_out, nand_58_out, nand_59_out, nand_60_out,
       nand_61_out, nand_62_out, nand_63_out, nand_64_out, nand_65_out, nand_66_out, nand_67_out,
       nand_68_out, nand_69_out, nand_70_out, nand_71_out, nand_72_out, nand_73_out, nand_74_out,
       nand_76_out, nand_77_out, nand_78_out, nand_79_out, nand_80_out, nand_81_out, nand_82_out,
       nand_83_out, nand_84_out, nand_85_out, nand_86_out, nand_87_out, nand_88_out, nand_89_out,
       nand_90_out, nand_91_out, nand_92_out, nand_93_out, nand_94_out, nand_95_out, nand_96_out,
       nand_99_out, nand_100_out, nand_101_out, nand_102_out, nand_103_out, nand_104_out, nand_105_out,
       nand_106_out, nand_107_out, nand_108_out, nand_109_out, nand_110_out, nand_111_out, nand_112_out,
       nand_113_out, nand_114_out, nand_115_out, nand_116_out, nand_117_out, nand_118_out, nand_119_out,
       nand_120_out, nand_121_out, nand_122_out, nand_123_out, nand_128_out, nand_130_out, nand_131_out,
       nand_132_out, nand_134_out, nand_135_out, nand_136_out, nand_137_out, nand_138_out, nand_139_out,
       nand_140_out, nand_141_out, nand_142_out, nand_143_out, nand_144_out, nand_145_out, nand_146_out,
       nand_147_out, nand_148_out, nand_149_out, nand_150_out, nand_151_out, nand_152_out, nand_153_out,
       nand_154_out, nand_155_out, nand_156_out, nand_157_out, nand_158_out, nand_159_out, nand_160_out,
       nand_161_out, nand_162_out, nand_163_out, nand_164_out, nand_165_out, nand_166_out, nand_167_out,
       nand_168_out, nand_169_out, nand_171_out, nand_174_out, nand_175_out, nand_176_out, nand_177_out,
       nand_178_out, nand_179_out, nand_180_out, nand_181_out, nand_182_out, nand_183_out, nand_184_out,
       nand_185_out, nand_186_out, nand_187_out, nand_188_out, nand_189_out, nand_190_out, nand_191_out,
       nand_192_out, nand_193_out, nand_194_out, nand_195_out, nand_196_out, nand_197_out, nand_198_out,
       nand_199_out, nand_200_out, nand_201_out, nand_202_out, nand_204_out, nand_205_out, nand_208_out,
       nand_209_out, nand_210_out, nand_215_out, nand_216_out, nand_217_out, nand_218_out, nand_219_out,
       nand_220_out, nand_221_out, nand_222_out, nand_223_out, nand_224_out, nand_225_out, nand_230_out,
       nand_231_out, nand_232_out, nand_233_out, nand_238_out, nand_239_out, nand_240_out, nand_241_out,
       nand_242_out, nand_243_out, nand_244_out, nand_245_out, nand_246_out, nand_247_out, nand_248_out,
       nand_249_out, nand_250_out, nand_251_out, nand_252_out, nand_253_out, nand_254_out, nand_255_out,
       nand_256_out, nand_257_out, nand_258_out, nand_259_out, nand_260_out, nand_261_out, nand_262_out,
       nand_263_out, nand_264_out, nand_265_out, nand_266_out, nand_267_out, nand_268_out, nand_269_out,
       nand_270_out, nand_271_out, nand_272_out, nand_273_out, nand_274_out, nand_275_out, nand_276_out,
       nand_277_out, nand_278_out, nand_279_out, nand_280_out, nand_281_out, nand_282_out, nand_286_out,
       nand_287_out, nand_288_out, nand_289_out, nand_290_out, nand_291_out, nand_292_out, nand_293_out,
       nand_294_out, nand_295_out, nand_296_out, nand_297_out, nand_298_out, nand_299_out, nand_300_out,
       nand_301_out, nand_302_out, nand_303_out, nand_304_out, nand_305_out, nand_306_out, nand_307_out,
       nand_308_out, nand_309_out, nand_310_out, nand_311_out, nand_312_out, nand_313_out, nand_314_out,
       nand_315_out, nand_316_out, nand_317_out, nand_318_out, nand_319_out, nand_320_out, nand_321_out,
       nand_322_out, nand_323_out, nand_324_out, nand_325_out, nand_326_out, nand_327_out, nand_328_out,
       nand_330_out, nand_331_out, nand_332_out, nand_333_out, nand_334_out, nand_335_out, nand_336_out,
       nand_337_out, nand_338_out, nand_339_out, nand_340_out, nand_341_out, nand_342_out, nand_343_out,
       nand_344_out, nand_345_out, nand_346_out, nand_347_out, nand_348_out, nand_349_out, nand_350_out,
       nand_351_out, nand_352_out, nand_353_out, nand_354_out, nand_355_out, nand_356_out, nand_357_out,
       nand_358_out, nand_359_out, nand_360_out, nand_361_out, nand_362_out, nand_363_out, nand_364_out,
       nand_365_out, nand_366_out, nand_367_out, nand_370_out, nand_373_out, nand_374_out, nand_375_out,
       nand_376_out, nand_377_out, nand_378_out, nand_379_out, nand_382_out, nand_385_out, nand_386_out,
       nand_387_out, nand_388_out, nand_389_out, nand_390_out, nand_391_out, nand_392_out, nand_393_out,
       nand_394_out, nand_395_out, nand_396_out, nand_397_out, nand_398_out, nand_399_out, nand_400_out,
       nand_401_out, nand_402_out, nand_403_out, nand_404_out, nand_405_out, nand_406_out, nand_407_out,
       nand_408_out, nand_411_out, nand_412_out, nand_413_out, nand_414_out, nand_415_out, nand_416_out,
       nand_419_out, nand_420_out, undriven, undriven_2, undriven_3, undriven_4, undriven_5, undriven_6,
       undriven_7, undriven_8, undriven_9, undriven_10, undriven_11, undriven_12, undriven_13, undriven_14,
       undriven_15, undriven_16;

  nand nand_1 (nand_1_out, undriven, undriven);
  nand nand_2 (nand_2_out, undriven_2, undriven_3);
  nand nand_3 (nand_3_out, undriven_4, undriven_5);
  nand nand_4 (nand_4_out, undriven_6, undriven_6);
  nand nand_5 (nand_5_out, undriven_12, undriven_12);
  nand nand_6 (nand_6_out, undriven_7, undriven_7);
  nand nand_7 (nand_7_out, undriven_13, undriven_13);
  nand nand_8 (nand_8_out, undriven_8, undriven_8);
  nand nand_9 (nand_9_out, undriven_14, undriven_14);
  nand nand_10 (nand_10_out, undriven_9, undriven_9);
  nand nand_11 (nand_11_out, undriven_15, undriven_15);
  nand nand_12 (nand_12_out, undriven_10, undriven_11);
  _2_1MUX u_2_1mux_1 (.I0(dflipflop_1_q), .I1(I), .S0(SHIFT), .Output(n2_1mux_1_output));
  nand nand_13 (nand_13_out, DIR_1______0, DIR_1______0);
  nand nand_14 (nand_14_out, Lin, DIR_1______0);
  nand nand_15 (nand_15_out, nand_3_out, nand_3_out);
  nand nand_16 (nand_16_out, nand_4_out, nand_5_out);
  nand nand_17 (nand_17_out, nand_6_out, nand_7_out);
  nand nand_18 (nand_18_out, undriven_8, nand_9_out);
  nand nand_19 (nand_19_out, nand_8_out, undriven_14);
  nand nand_20 (nand_20_out, undriven_9, nand_11_out);
  nand nand_21 (nand_21_out, nand_10_out, undriven_15);
  nand nand_22 (nand_22_out, nand_12_out, nand_12_out);
  nand nand_23 (nand_23_out, Clk_7, EN_3);
  DFlipFlop dflipflop_1 (
    .D(n2_1mux_1_output), .Clk(Clk_8), .Q(dflipflop_1_q), .PRE_prime(PRE_prime_8), .CLR_prime(CLR_prime_8));  // open: Q_prime
  nand nand_24 (nand_24_out, nand_13_out, dflipflop_14_q);
  nand nand_25 (nand_25_out, nand_14_out, nand_24_out);
  nand nand_26 (nand_26_out, DIR_1______0_2, DIR_1______0_2);
  nand nand_27 (nand_27_out, Lin_2, DIR_1______0_2);
  nand nand_28 (nand_28_out, nand_26_out, PRE_prime_10);
  nand nand_29 (nand_29_out, nand_27_out, nand_28_out);
  nand nand_30 (nand_30_out, nand_17_out, nand_17_out);
  nand nand_31 (nand_31_out, nand_18_out, nand_19_out);
  nand nand_32 (nand_32_out, nand_20_out, nand_21_out);
  nand nand_33 (nand_33_out, nand_22_out, undriven_16);
  _2_1MUX u_2_1mux_2 (.I0(O), .I1(DATA), .S0(LOAD), .Output(n2_1mux_2_output));
  _2_1MUX u_2_1mux_3 (.I0(O_6), .I1(D0), .S0(LOAD_2), .Output(n2_1mux_3_output));
  _2_1MUX u_2_1mux_4 (.I0(O_7), .I1(D1), .S0(LOAD_2), .Output(n2_1mux_4_output));
  _2_1MUX u_2_1mux_5 (.I0(O_8), .I1(D2), .S0(LOAD_2), .Output(n2_1mux_5_output));
  _2_1MUX u_2_1mux_6 (.I0(O_9), .I1(D3), .S0(LOAD_2), .Output(n2_1mux_6_output));
  nand nand_34 (nand_34_out, nand_23_out, nand_23_out);
  _2_1MUX u_2_1mux_7 (.I0(O_10), .I1(D0_2), .S0(LOAD_3), .Output(n2_1mux_7_output));
  _2_1MUX u_2_1mux_8 (.I0(O_11), .I1(D1_2), .S0(LOAD_3), .Output(n2_1mux_8_output));
  _2_1MUX u_2_1mux_9 (.I0(O_12), .I1(D2_2), .S0(LOAD_3), .Output(n2_1mux_9_output));
  _2_1MUX u_2_1mux_10 (.I0(O_13), .I1(D3_2), .S0(LOAD_3), .Output(n2_1mux_10_output));
  _2_1MUX u_2_1mux_11 (.I0(dflipflop_12_q), .I1(dflipflop_1_q), .S0(SHIFT), .Output(n2_1mux_11_output));
  nand nand_35 (nand_35_out, Lout, DIR_1______0);
  _2_1MUX u_2_1mux_12 (.I0(Lout), .I1(nand_25_out), .S0(SHIFT_2), .Output(n2_1mux_12_output));
  DFlipFlop dflipflop_2 (
    .D(n2_1mux_12_output), .Clk(Clk_9), .Q(Lout), .PRE_prime(PRE_prime_9), .CLR_prime(CLR_prime_9));  // open: Q_prime
  _2_1MUX u_2_1mux_13 (.I0(dflipflop_15_q), .I1(nand_29_out), .S0(SHIFT_3), .Output(n2_1mux_13_output));
  nand nand_36 (nand_36_out, nand_131_out, dflipflop_15_q);
  nand nand_37 (nand_37_out, nand_32_out, nand_32_out);
  DFlipFlop dflipflop_3 (
    .D(n2_1mux_2_output), .Clk(Clk_4), .Q(O), .PRE_prime(PRE_prime_4), .CLR_prime(CLR_prime_4));  // open: Q_prime
  DFlipFlop dflipflop_4 (
    .D(n2_1mux_3_output), .Clk(Clk_6), .Q(O_6), .PRE_prime(PRE_prime_6), .CLR_prime(CLR_prime_5));  // open: Q_prime
  DFlipFlop dflipflop_5 (
    .D(n2_1mux_4_output), .Clk(Clk_6), .Q(O_7), .PRE_prime(PRE_prime_6), .CLR_prime(CLR_prime_5));  // open: Q_prime
  DFlipFlop dflipflop_6 (
    .D(n2_1mux_5_output), .Clk(Clk_6), .Q(O_8), .PRE_prime(PRE_prime_6), .CLR_prime(CLR_prime_5));  // open: Q_prime
  DFlipFlop dflipflop_7 (
    .D(n2_1mux_6_output), .Clk(Clk_6), .Q(O_9), .PRE_prime(PRE_prime_6), .CLR_prime(CLR_prime_5));  // open: Q_prime
  DFlipFlop dflipflop_8 (
    .D(n2_1mux_7_output), .Clk(nand_34_out), .Q(O_10), .PRE_prime(PRE_prime_7), .CLR_prime(CLR_prime_7));  // open: Q_prime
  DFlipFlop dflipflop_9 (
    .D(n2_1mux_8_output), .Clk(nand_34_out), .Q(O_11), .PRE_prime(PRE_prime_7), .CLR_prime(CLR_prime_7));  // open: Q_prime
  DFlipFlop dflipflop_10 (
    .D(n2_1mux_9_output), .Clk(nand_34_out), .Q(O_12), .PRE_prime(PRE_prime_7), .CLR_prime(CLR_prime_7));  // open: Q_prime
  DFlipFlop dflipflop_11 (
    .D(n2_1mux_10_output), .Clk(nand_34_out), .Q(O_13), .PRE_prime(PRE_prime_7), .CLR_prime(CLR_prime_7));  // open: Q_prime
  DFlipFlop dflipflop_12 (
    .D(n2_1mux_11_output), .Clk(Clk_8), .Q(dflipflop_12_q), .PRE_prime(PRE_prime_8), .CLR_prime(CLR_prime_8));  // open: Q_prime
  nand nand_38 (nand_38_out, nand_13_out, dflipflop_17_q);
  nand nand_39 (nand_39_out, nand_35_out, nand_38_out);
  _2_1MUX u_2_1mux_14 (
    .I0(n2_1mux_13_output), .I1(P3), .S0(INPUT_MODE_1_ParallelIn__0_SerialIn), .Output(n2_1mux_14_output));
  nand nand_40 (Lout_2, nand_36_out, nand_36_out);
  nand nand_41 (nand_41_out, OUTPUT_MODE_Parallel_1__Serial_0, dflipflop_15_q);
  nand nand_42 (O3_3, nand_41_out, nand_41_out);
  _2_1MUX u_2_1mux_15 (.I0(dflipflop_13_q), .I1(dflipflop_12_q), .S0(SHIFT), .Output(n2_1mux_15_output));
  DFlipFlop dflipflop_13 (
    .D(n2_1mux_15_output), .Clk(Clk_8), .Q(dflipflop_13_q), .PRE_prime(PRE_prime_8), .CLR_prime(CLR_prime_8));  // open: Q_prime
  DFlipFlop dflipflop_14 (
    .D(n2_1mux_16_output), .Clk(Clk_9), .Q(dflipflop_14_q), .PRE_prime(PRE_prime_9), .CLR_prime(CLR_prime_9));  // open: Q_prime
  _2_1MUX u_2_1mux_16 (.I0(dflipflop_14_q), .I1(nand_39_out), .S0(SHIFT_2), .Output(n2_1mux_16_output));
  nand nand_43 (nand_43_out, nand_26_out, dflipflop_20_q);
  nand nand_44 (nand_44_out, dflipflop_15_q, DIR_1______0_2);
  nand nand_45 (nand_45_out, nand_44_out, nand_43_out);
  DFlipFlop dflipflop_15 (
    .D(n2_1mux_14_output), .Clk(Clk_10), .Q(dflipflop_15_q), .PRE_prime(PRE_prime_10),
    .CLR_prime(CLR_prime_10));  // open: Q_prime
  _2_1MUX u_2_1mux_17 (.I0(O_14), .I1(dflipflop_13_q), .S0(SHIFT), .Output(n2_1mux_17_output));
  nand nand_46 (nand_46_out, nand_13_out, Rout);
  nand nand_47 (nand_47_out, dflipflop_14_q, DIR_1______0);
  nand nand_48 (nand_48_out, nand_47_out, nand_46_out);
  _2_1MUX u_2_1mux_18 (.I0(dflipflop_18_q), .I1(nand_45_out), .S0(SHIFT_3), .Output(n2_1mux_18_output));
  _2_1MUX u_2_1mux_19 (
    .I0(n2_1mux_18_output), .I1(P2), .S0(INPUT_MODE_1_ParallelIn__0_SerialIn), .Output(n2_1mux_19_output));
  DFlipFlop dflipflop_16 (
    .D(n2_1mux_17_output), .Clk(Clk_8), .Q(O_14), .PRE_prime(PRE_prime_8), .CLR_prime(CLR_prime_8));  // open: Q_prime
  DFlipFlop dflipflop_17 (
    .D(n2_1mux_20_output), .Clk(Clk_9), .Q(dflipflop_17_q), .PRE_prime(PRE_prime_9), .CLR_prime(CLR_prime_9));  // open: Q_prime
  _2_1MUX u_2_1mux_20 (.I0(dflipflop_17_q), .I1(nand_48_out), .S0(SHIFT_2), .Output(n2_1mux_20_output));
  nand nand_49 (nand_49_out, dflipflop_18_q, DIR_1______0_2);
  DFlipFlop dflipflop_18 (
    .D(n2_1mux_19_output), .Clk(Clk_10), .Q(dflipflop_18_q), .PRE_prime(PRE_prime_10),
    .CLR_prime(CLR_prime_10));  // open: Q_prime
  nand nand_50 (nand_50_out, OUTPUT_MODE_Parallel_1__Serial_0, dflipflop_18_q);
  nand nand_51 (O2_3, nand_50_out, nand_50_out);
  nand nand_52 (nand_52_out, A, A);
  nand nand_53 (nand_53_out, B, B);
  nand nand_54 (nand_54_out, A, B);
  nand nand_55 (nand_55_out, A_3, A_3);
  nand nand_56 (nand_56_out, B_3, B_3);
  nand nand_57 (nand_57_out, A_3, B_3);
  nand nand_58 (nand_58_out, A_3, A_3);
  nand nand_59 (nand_59_out, B_3, B_3);
  nand nand_60 (nand_60_out, A0, A0);
  nand nand_61 (nand_61_out, B0, B0);
  nand nand_62 (nand_62_out, A0, B0);
  nand nand_63 (nand_63_out, A0, A0);
  nand nand_64 (nand_64_out, B0, B0);
  nand nand_65 (nand_65_out, A2_2, A2_2);
  nand nand_66 (nand_66_out, B2_2, B2_2);
  nand nand_67 (nand_67_out, A2_2, B2_2);
  nand nand_68 (nand_68_out, A2_2, A2_2);
  nand nand_69 (nand_69_out, B2_2, B2_2);
  nand nand_70 (nand_70_out, nand_13_out, Rin);
  nand nand_71 (nand_71_out, dflipflop_17_q, DIR_1______0);
  nand nand_72 (nand_72_out, nand_71_out, nand_70_out);
  nand nand_73 (nand_73_out, nand_26_out, dflipflop_21_q);
  nand nand_74 (nand_74_out, nand_49_out, nand_73_out);
  _2_1MUX u_2_1mux_21 (.I0(dflipflop_20_q), .I1(nand_74_out), .S0(SHIFT_3), .Output(n2_1mux_21_output));
  nand nand_75 (C, nand_54_out, nand_54_out);
  nand nand_76 (nand_76_out, A_3, nand_56_out);
  nand nand_77 (nand_77_out, nand_55_out, B_3);
  nand nand_78 (nand_78_out, nand_57_out, nand_57_out);
  nand nand_79 (nand_79_out, nand_58_out, nand_59_out);
  nand nand_80 (nand_80_out, A0, nand_61_out);
  nand nand_81 (nand_81_out, nand_60_out, B0);
  nand nand_82 (nand_82_out, nand_62_out, nand_62_out);
  nand nand_83 (nand_83_out, nand_63_out, nand_64_out);
  nand nand_84 (nand_84_out, A2_2, nand_66_out);
  nand nand_85 (nand_85_out, nand_65_out, B2_2);
  nand nand_86 (nand_86_out, nand_67_out, nand_67_out);
  nand nand_87 (nand_87_out, nand_68_out, nand_69_out);
  _2_1MUX u_2_1mux_22 (.I0(Rout), .I1(nand_72_out), .S0(SHIFT_2), .Output(n2_1mux_22_output));
  DFlipFlop dflipflop_19 (
    .D(n2_1mux_22_output), .Clk(Clk_9), .Q(Rout), .PRE_prime(PRE_prime_9), .CLR_prime(CLR_prime_9));  // open: Q_prime
  _2_1MUX u_2_1mux_23 (.I0(n2_1mux_21_output), .I1(P1), .S0(INPUT_MODE_1_ParallelIn__0_SerialIn));  // open: Output
  nand nand_88 (nand_88_out, A, nand_53_out);
  nand nand_89 (nand_89_out, nand_52_out, B);
  nand nand_90 (nand_90_out, nand_79_out, Cin);
  nand nand_91 (nand_91_out, nand_83_out, Cin_2);
  nand nand_92 (nand_92_out, nand_84_out, nand_85_out);
  nand nand_93 (nand_93_out, nand_87_out, nand_171_out);
  nand nand_94 (nand_94_out, dflipflop_20_q, DIR_1______0_2);
  nand nand_95 (nand_95_out, nand_94_out, nand_104_out);
  DFlipFlop dflipflop_20 (
    .Clk(Clk_10), .Q(dflipflop_20_q), .PRE_prime(PRE_prime_10), .CLR_prime(CLR_prime_10));  // open: D, Q_prime
  nand nand_96 (nand_96_out, OUTPUT_MODE_Parallel_1__Serial_0, dflipflop_20_q);
  nand nand_97 (O1_5, nand_96_out, nand_96_out);
  nand nand_98 (S_2, nand_88_out, nand_89_out);
  nand nand_99 (nand_99_out, nand_76_out, nand_77_out);
  nand nand_100 (nand_100_out, nand_90_out, nand_90_out);
  nand nand_101 (nand_101_out, nand_80_out, nand_81_out);
  nand nand_102 (nand_102_out, nand_91_out, nand_91_out);
  nand nand_103 (nand_103_out, nand_93_out, nand_93_out);
  nand nand_104 (nand_104_out, nand_26_out, Rin_2);
  _2_1MUX u_2_1mux_24 (.I0(dflipflop_21_q), .I1(nand_95_out), .S0(SHIFT_3), .Output(n2_1mux_24_output));
  nand nand_105 (nand_105_out, nand_99_out, nand_99_out);
  nand nand_106 (nand_106_out, Cin, Cin);
  nand nand_107 (nand_107_out, nand_101_out, nand_101_out);
  nand nand_108 (nand_108_out, Cin_2, Cin_2);
  nand nand_109 (nand_109_out, nand_92_out, nand_92_out);
  nand nand_110 (nand_110_out, nand_171_out, nand_171_out);
  _2_1MUX u_2_1mux_25 (
    .I0(n2_1mux_24_output), .I1(P0), .S0(INPUT_MODE_1_ParallelIn__0_SerialIn), .Output(n2_1mux_25_output));
  nand nand_111 (nand_111_out, nand_99_out, nand_106_out);
  nand nand_112 (nand_112_out, nand_105_out, Cin);
  nand nand_113 (nand_113_out, nand_78_out, nand_78_out);
  nand nand_114 (nand_114_out, nand_100_out, nand_100_out);
  nand nand_115 (nand_115_out, nand_101_out, nand_108_out);
  nand nand_116 (nand_116_out, nand_107_out, Cin_2);
  nand nand_117 (nand_117_out, nand_82_out, nand_82_out);
  nand nand_118 (nand_118_out, nand_102_out, nand_102_out);
  nand nand_119 (nand_119_out, nand_92_out, nand_110_out);
  nand nand_120 (nand_120_out, nand_109_out, nand_171_out);
  nand nand_121 (nand_121_out, nand_86_out, nand_86_out);
  nand nand_122 (nand_122_out, nand_103_out, nand_103_out);
  DFlipFlop dflipflop_21 (
    .D(n2_1mux_25_output), .Clk(Clk_10), .Q(dflipflop_21_q), .PRE_prime(PRE_prime_10),
    .CLR_prime(CLR_prime_10));  // open: Q_prime
  nand nand_123 (nand_123_out, OUTPUT_MODE_Parallel_1__Serial_0, dflipflop_21_q);
  nand nand_124 (O0_6, nand_123_out, nand_123_out);
  nand nand_125 (S_3, nand_111_out, nand_112_out);
  nand nand_126 (C_2, nand_113_out, nand_114_out);
  nand nand_127 (S0_4, nand_115_out, nand_116_out);
  nand nand_128 (nand_128_out, nand_117_out, nand_118_out);
  nand nand_129 (S2, nand_119_out, nand_120_out);
  nand nand_130 (nand_130_out, nand_121_out, nand_122_out);
  nand nand_131 (nand_131_out, OUTPUT_MODE_Parallel_1__Serial_0, OUTPUT_MODE_Parallel_1__Serial_0);
  TFlipFlop tflipflop_1 (
    .T(LOGIC1_2), .Clk(Clk_5), .Q(O_2), .PRE_prime(PRE_prime_5), .CLR_prime(CLR_prime_6));  // open: Q_prime
  nand nand_132 (nand_132_out, dflipflop_21_q, nand_131_out);
  TFlipFlop tflipflop_2 (
    .T(LOGIC1_2), .Clk(O_2), .Q(O_3), .PRE_prime(PRE_prime_5), .CLR_prime(CLR_prime_6));  // open: Q_prime
  nand nand_133 (Rout_2, nand_132_out, nand_132_out);
  TFlipFlop tflipflop_3 (
    .T(LOGIC1_2), .Clk(O_3), .Q(O_4), .PRE_prime(PRE_prime_5), .CLR_prime(CLR_prime_6));  // open: Q_prime
  TFlipFlop tflipflop_4 (
    .T(LOGIC1_2), .Clk(O_4), .Q(O_5), .PRE_prime(PRE_prime_5), .CLR_prime(CLR_prime_6));  // open: Q_prime
  nand nand_134 (nand_134_out, A1, A1);
  nand nand_135 (nand_135_out, B1, B1);
  nand nand_136 (nand_136_out, A1, B1);
  nand nand_137 (nand_137_out, A1, A1);
  nand nand_138 (nand_138_out, B1, B1);
  nand nand_139 (nand_139_out, A3_2, A3_2);
  nand nand_140 (nand_140_out, B3_2, B3_2);
  nand nand_141 (nand_141_out, A3_2, B3_2);
  nand nand_142 (nand_142_out, A3_2, A3_2);
  nand nand_143 (nand_143_out, B3_2, B3_2);
  nand nand_144 (nand_144_out, A1, nand_135_out);
  nand nand_145 (nand_145_out, nand_134_out, B1);
  nand nand_146 (nand_146_out, nand_136_out, nand_136_out);
  nand nand_147 (nand_147_out, nand_137_out, nand_138_out);
  nand nand_148 (nand_148_out, A3_2, nand_140_out);
  nand nand_149 (nand_149_out, nand_139_out, B3_2);
  nand nand_150 (nand_150_out, nand_141_out, nand_141_out);
  nand nand_151 (nand_151_out, nand_142_out, nand_143_out);
  nand nand_152 (nand_152_out, nand_147_out, nand_128_out);
  nand nand_153 (nand_153_out, nand_148_out, nand_149_out);
  nand nand_154 (nand_154_out, nand_151_out, nand_130_out);
  nand nand_155 (nand_155_out, nand_144_out, nand_145_out);
  nand nand_156 (nand_156_out, nand_152_out, nand_152_out);
  nand nand_157 (nand_157_out, nand_154_out, nand_154_out);
  nand nand_158 (nand_158_out, nand_155_out, nand_155_out);
  nand nand_159 (nand_159_out, nand_128_out, nand_128_out);
  nand nand_160 (nand_160_out, nand_153_out, nand_153_out);
  nand nand_161 (nand_161_out, nand_130_out, nand_130_out);
  nand nand_162 (nand_162_out, nand_155_out, nand_159_out);
  nand nand_163 (nand_163_out, nand_158_out, nand_128_out);
  nand nand_164 (nand_164_out, nand_146_out, nand_146_out);
  nand nand_165 (nand_165_out, nand_156_out, nand_156_out);
  nand nand_166 (nand_166_out, nand_153_out, nand_161_out);
  nand nand_167 (nand_167_out, nand_160_out, nand_130_out);
  nand nand_168 (nand_168_out, nand_150_out, nand_150_out);
  nand nand_169 (nand_169_out, nand_157_out, nand_157_out);
  nand nand_170 (S1_3, nand_162_out, nand_163_out);
  nand nand_171 (nand_171_out, nand_164_out, nand_165_out);
  nand nand_172 (S3, nand_166_out, nand_167_out);
  nand nand_173 (Cout, nand_168_out, nand_169_out);
  nand nand_174 (nand_174_out, S0, S0);
  nand nand_175 (nand_175_out, S0_2, S0_2);
  nand nand_176 (nand_176_out, S0_2, S0_2);
  nand nand_177 (nand_177_out, O0, O0);
  nand nand_178 (nand_178_out, S1_2, S1_2);
  nand nand_179 (nand_179_out, I2_2, I2_2);
  nand nand_180 (nand_180_out, I3_2, I3_2);
  nand nand_181 (nand_181_out, I2_2, I2_2);
  nand nand_182 (nand_182_out, I1_3, I1_3);
  nand nand_183 (nand_183_out, I0_5, I0_5);
  nand nand_184 (nand_184_out, I0_6, I0_6);
  nand nand_185 (nand_185_out, I1_4, I1_4);
  nand nand_186 (nand_186_out, I0, nand_174_out);
  nand nand_187 (nand_187_out, I1, S0);
  nand nand_188 (nand_188_out, I0_2, nand_175_out);
  nand nand_189 (nand_189_out, I1_2, S0_2);
  nand nand_190 (nand_190_out, I2, nand_176_out);
  nand nand_191 (nand_191_out, I3, S0_2);
  nand nand_192 (nand_192_out, I0_3, nand_177_out);
  nand nand_193 (nand_193_out, I0_3, O0);
  nand nand_194 (nand_194_out, I0_4, nand_178_out);
  nand nand_195 (nand_195_out, I0_4, S1_2);
  nand nand_196 (nand_196_out, I1_3, nand_179_out);
  nand nand_197 (nand_197_out, nand_180_out, nand_181_out);
  nand nand_198 (nand_198_out, nand_182_out, nand_183_out);
  nand nand_199 (nand_199_out, nand_184_out, nand_185_out);
  nand nand_200 (nand_200_out, I0_6, nand_185_out);
  nand nand_201 (nand_201_out, nand_184_out, I1_4);
  nand nand_202 (nand_202_out, I0_6, I1_4);
  nand nand_203 (Output, nand_186_out, nand_187_out);
  nand nand_204 (nand_204_out, nand_188_out, nand_189_out);
  nand nand_205 (nand_205_out, nand_190_out, nand_191_out);
  nand nand_206 (O0_2, nand_192_out, nand_192_out);
  nand nand_207 (O1, nand_193_out, nand_193_out);
  nand nand_208 (nand_208_out, nand_194_out, nand_194_out);
  nand nand_209 (nand_209_out, nand_195_out, nand_195_out);
  nand nand_210 (nand_210_out, nand_196_out, nand_196_out);
  nand nand_211 (O0_5, nand_199_out, nand_199_out);
  nand nand_212 (O1_4, nand_200_out, nand_200_out);
  nand nand_213 (O2_2, nand_201_out, nand_201_out);
  nand nand_214 (O3_2, nand_202_out, nand_202_out);
  nand nand_215 (nand_215_out, S1, S1);
  nand nand_216 (nand_216_out, nand_210_out, nand_210_out);
  nand nand_217 (nand_217_out, I3_2, I3_2);
  nand nand_218 (nand_218_out, I2_2, I2_2);
  nand nand_219 (nand_219_out, I3_2, I3_2);
  nand nand_220 (nand_220_out, nand_197_out, nand_197_out);
  nand nand_221 (nand_221_out, nand_198_out, nand_198_out);
  nand nand_222 (nand_222_out, nand_204_out, nand_215_out);
  nand nand_223 (nand_223_out, nand_205_out, S1);
  nand nand_224 (nand_224_out, S0_3, S0_3);
  nand nand_225 (nand_225_out, S0_3, S0_3);
  nand nand_226 (O0_4, nand_216_out, nand_217_out);
  nand nand_227 (O1_3, nand_218_out, nand_219_out);
  nand nand_228 (Valid, nand_220_out, nand_221_out);
  nand nand_229 (Output_2, nand_222_out, nand_223_out);
  nand nand_230 (nand_230_out, nand_208_out, nand_224_out);
  nand nand_231 (nand_231_out, nand_208_out, S0_3);
  nand nand_232 (nand_232_out, nand_209_out, nand_225_out);
  nand nand_233 (nand_233_out, nand_209_out, S0_3);
  nand nand_234 (O0_3, nand_230_out, nand_230_out);
  nand nand_235 (O1_2, nand_231_out, nand_231_out);
  nand nand_236 (O2, nand_232_out, nand_232_out);
  nand nand_237 (O3, nand_233_out, nand_233_out);
  nand nand_238 (nand_238_out, A_2, A_2);
  nand nand_239 (nand_239_out, B_2, B_2);
  nand nand_240 (nand_240_out, A3, A3);
  nand nand_241 (nand_241_out, B3, B3);
  nand nand_242 (nand_242_out, A2, A2);
  nand nand_243 (nand_243_out, B2, B2);
  nand nand_244 (nand_244_out, A1_2, A1_2);
  nand nand_245 (nand_245_out, B1_2, B1_2);
  nand nand_246 (nand_246_out, A0_2, A0_2);
  nand nand_247 (nand_247_out, B0_2, B0_2);
  nand nand_248 (nand_248_out, A_2, A_2);
  nand nand_249 (nand_249_out, A_2, nand_239_out);
  nand nand_250 (nand_250_out, nand_238_out, B_2);
  nand nand_251 (nand_251_out, B_2, B_2);
  nand nand_252 (nand_252_out, A3, A3);
  nand nand_253 (nand_253_out, A3, nand_241_out);
  nand nand_254 (nand_254_out, nand_240_out, B3);
  nand nand_255 (nand_255_out, B3, B3);
  nand nand_256 (nand_256_out, A2, A2);
  nand nand_257 (nand_257_out, A2, nand_243_out);
  nand nand_258 (nand_258_out, nand_242_out, B2);
  nand nand_259 (nand_259_out, B2, B2);
  nand nand_260 (nand_260_out, A1_2, A1_2);
  nand nand_261 (nand_261_out, A1_2, nand_245_out);
  nand nand_262 (nand_262_out, nand_244_out, B1_2);
  nand nand_263 (nand_263_out, B1_2, B1_2);
  nand nand_264 (nand_264_out, A0_2, A0_2);
  nand nand_265 (nand_265_out, A0_2, nand_247_out);
  nand nand_266 (nand_266_out, nand_246_out, B0_2);
  nand nand_267 (nand_267_out, B0_2, B0_2);
  nand nand_268 (nand_268_out, nand_248_out, A_2);
  nand nand_269 (nand_269_out, nand_249_out, nand_250_out);
  nand nand_270 (nand_270_out, B_2, nand_251_out);
  nand nand_271 (nand_271_out, nand_252_out, A3);
  nand nand_272 (nand_272_out, nand_253_out, nand_254_out);
  nand nand_273 (nand_273_out, B3, nand_255_out);
  nand nand_274 (nand_274_out, nand_256_out, A2);
  nand nand_275 (nand_275_out, nand_257_out, nand_258_out);
  nand nand_276 (nand_276_out, B2, nand_259_out);
  nand nand_277 (nand_277_out, nand_260_out, A1_2);
  nand nand_278 (nand_278_out, nand_261_out, nand_262_out);
  nand nand_279 (nand_279_out, B1_2, nand_263_out);
  nand nand_280 (nand_280_out, nand_264_out, A0_2);
  nand nand_281 (nand_281_out, nand_265_out, nand_266_out);
  nand nand_282 (nand_282_out, B0_2, nand_267_out);
  nand nand_283 (L_A_B, nand_268_out, nand_268_out);
  nand nand_284 (E, nand_269_out, nand_269_out);
  nand nand_285 (G_A_B, nand_270_out, nand_270_out);
  nand nand_286 (nand_286_out, nand_271_out, nand_271_out);
  nand nand_287 (nand_287_out, nand_272_out, nand_272_out);
  nand nand_288 (nand_288_out, nand_273_out, nand_273_out);
  nand nand_289 (nand_289_out, nand_274_out, nand_274_out);
  nand nand_290 (nand_290_out, nand_275_out, nand_275_out);
  nand nand_291 (nand_291_out, nand_276_out, nand_276_out);
  nand nand_292 (nand_292_out, nand_277_out, nand_277_out);
  nand nand_293 (nand_293_out, nand_278_out, nand_278_out);
  nand nand_294 (nand_294_out, nand_279_out, nand_279_out);
  nand nand_295 (nand_295_out, nand_280_out, nand_280_out);
  nand nand_296 (nand_296_out, nand_281_out, nand_281_out);
  nand nand_297 (nand_297_out, nand_282_out, nand_282_out);
  nand nand_298 (nand_298_out, nand_287_out, nand_287_out);
  nand nand_299 (nand_299_out, nand_290_out, nand_290_out);
  nand nand_300 (nand_300_out, nand_293_out, nand_293_out);
  nand nand_301 (nand_301_out, nand_296_out, nand_296_out);
  nand nand_302 (nand_302_out, LOGIC1, nand_298_out);
  nand nand_303 (nand_303_out, LOGIC1, nand_287_out);
  nand nand_304 (nand_304_out, LOGIC1, nand_299_out);
  nand nand_305 (nand_305_out, LOGIC1, nand_290_out);
  nand nand_306 (nand_306_out, LOGIC1, nand_300_out);
  nand nand_307 (nand_307_out, LOGIC1, nand_293_out);
  nand nand_308 (nand_308_out, LOGIC1, nand_301_out);
  nand nand_309 (nand_309_out, LOGIC1, nand_296_out);
  nand nand_310 (nand_310_out, nand_302_out, nand_302_out);
  nand nand_311 (nand_311_out, nand_303_out, nand_303_out);
  nand nand_312 (nand_312_out, nand_304_out, nand_304_out);
  nand nand_313 (nand_313_out, nand_305_out, nand_305_out);
  nand nand_314 (nand_314_out, nand_306_out, nand_306_out);
  nand nand_315 (nand_315_out, nand_307_out, nand_307_out);
  nand nand_316 (nand_316_out, nand_308_out, nand_308_out);
  nand nand_317 (nand_317_out, nand_309_out, nand_309_out);
  nand nand_318 (nand_318_out, nand_311_out, nand_312_out);
  nand nand_319 (nand_319_out, nand_311_out, nand_313_out);
  nand nand_320 (nand_320_out, nand_325_out, nand_314_out);
  nand nand_321 (nand_321_out, nand_325_out, nand_315_out);
  nand nand_322 (nand_322_out, nand_327_out, nand_316_out);
  nand nand_323 (nand_323_out, nand_327_out, nand_317_out);
  nand nand_324 (nand_324_out, nand_318_out, nand_318_out);
  nand nand_325 (nand_325_out, nand_319_out, nand_319_out);
  nand nand_326 (nand_326_out, nand_320_out, nand_320_out);
  nand nand_327 (nand_327_out, nand_321_out, nand_321_out);
  nand nand_328 (nand_328_out, nand_322_out, nand_322_out);
  nand nand_329 (E_2, nand_323_out, nand_323_out);
  nand nand_330 (nand_330_out, nand_286_out, nand_286_out);
  nand nand_331 (nand_331_out, nand_289_out, nand_289_out);
  nand nand_332 (nand_332_out, nand_292_out, nand_292_out);
  nand nand_333 (nand_333_out, nand_295_out, nand_295_out);
  nand nand_334 (nand_334_out, nand_310_out, nand_310_out);
  nand nand_335 (nand_335_out, nand_324_out, nand_324_out);
  nand nand_336 (nand_336_out, nand_326_out, nand_326_out);
  nand nand_337 (nand_337_out, nand_328_out, nand_328_out);
  nand nand_338 (nand_338_out, nand_330_out, nand_331_out);
  nand nand_339 (nand_339_out, nand_332_out, nand_333_out);
  nand nand_340 (nand_340_out, nand_334_out, nand_335_out);
  nand nand_341 (nand_341_out, nand_336_out, nand_337_out);
  nand nand_342 (nand_342_out, nand_288_out, nand_288_out);
  nand nand_343 (nand_343_out, nand_291_out, nand_291_out);
  nand nand_344 (nand_344_out, nand_294_out, nand_294_out);
  nand nand_345 (nand_345_out, nand_297_out, nand_297_out);
  nand nand_346 (nand_346_out, nand_310_out, nand_310_out);
  nand nand_347 (nand_347_out, nand_324_out, nand_324_out);
  nand nand_348 (nand_348_out, nand_326_out, nand_326_out);
  nand nand_349 (nand_349_out, nand_328_out, nand_328_out);
  nand nand_350 (nand_350_out, nand_342_out, nand_343_out);
  nand nand_351 (nand_351_out, nand_344_out, nand_345_out);
  nand nand_352 (nand_352_out, nand_346_out, nand_347_out);
  nand nand_353 (nand_353_out, nand_348_out, nand_349_out);
  nand nand_354 (nand_354_out, nand_338_out, nand_338_out);
  nand nand_355 (nand_355_out, nand_339_out, nand_339_out);
  nand nand_356 (nand_356_out, nand_340_out, nand_340_out);
  nand nand_357 (nand_357_out, nand_341_out, nand_341_out);
  nand nand_358 (nand_358_out, nand_350_out, nand_350_out);
  nand nand_359 (nand_359_out, nand_351_out, nand_351_out);
  nand nand_360 (nand_360_out, nand_352_out, nand_352_out);
  nand nand_361 (nand_361_out, nand_353_out, nand_353_out);
  nand nand_362 (nand_362_out, nand_354_out, nand_355_out);
  nand nand_363 (nand_363_out, nand_356_out, nand_357_out);
  nand nand_364 (nand_364_out, nand_358_out, nand_359_out);
  nand nand_365 (nand_365_out, nand_360_out, nand_361_out);
  nand nand_366 (nand_366_out, nand_362_out, nand_363_out);
  nand nand_367 (nand_367_out, nand_364_out, nand_365_out);
  nand nand_368 (L_A_B_2, nand_366_out, nand_366_out);
  nand nand_369 (G_A_B_2, nand_367_out, nand_367_out);
  nand nand_370 (nand_370_out, D, D);
  nand nand_371 (Q, S_prime, Q_prime);
  nand nand_372 (Q_prime, Q, R_prime);
  nand nand_373 (nand_373_out, S, EN);
  nand nand_374 (nand_374_out, EN, R);
  nand nand_375 (nand_375_out, D_2, D_2);
  nand nand_376 (nand_376_out, Clk, Clk);
  nand nand_377 (nand_377_out, Q_5, Q_5);
  nand nand_378 (nand_378_out, T, T);
  nand nand_379 (nand_379_out, K, K);
  nand nand_380 (Q_2, nand_373_out, Q_prime_2);
  nand nand_381 (Q_prime_2, Q_2, nand_374_out);
  nand nand_382 (nand_382_out, D, EN_2);
  nand nand_383 (Q_3, nand_382_out, Q_prime_3);
  nand nand_384 (Q_prime_3, Q_3, nand_385_out);
  nand nand_385 (nand_385_out, EN_2, nand_370_out);
  nand nand_386 (nand_386_out, Q_5, nand_378_out);
  nand nand_387 (nand_387_out, nand_377_out, T);
  nand nand_388 (nand_388_out, Q_prime_6, J);
  nand nand_389 (nand_389_out, Q_6, nand_379_out);
  nand nand_390 (nand_390_out, D_2, nand_376_out);
  nand nand_391 (nand_391_out, nand_376_out, nand_375_out);
  nand nand_392 (nand_392_out, nand_386_out, nand_387_out);
  nand nand_393 (nand_393_out, nand_388_out, nand_389_out);
  nand nand_394 (nand_394_out, nand_390_out, nand_396_out);
  nand nand_395 (nand_395_out, nand_394_out, nand_394_out);
  nand nand_396 (nand_396_out, nand_394_out, nand_391_out);
  nand nand_397 (nand_397_out, nand_392_out, nand_392_out);
  nand nand_398 (nand_398_out, Clk_2, Clk_2);
  nand nand_399 (nand_399_out, nand_392_out, nand_398_out);
  nand nand_400 (nand_400_out, nand_398_out, nand_397_out);
  nand nand_401 (nand_401_out, nand_393_out, nand_393_out);
  nand nand_402 (nand_402_out, Clk_3, Clk_3);
  nand nand_403 (nand_403_out, nand_394_out, Clk);
  nand nand_404 (nand_404_out, Clk, nand_395_out);
  nand nand_405 (nand_405_out, nand_399_out, nand_406_out);
  nand nand_406 (nand_406_out, nand_405_out, nand_400_out);
  nand nand_407 (nand_407_out, nand_393_out, nand_402_out);
  nand nand_408 (nand_408_out, nand_402_out, nand_401_out);
  nand nand_409 (Q_4, nand_403_out, PRE_prime, Q_prime_4);
  nand nand_410 (Q_prime_4, Q_4, CLR_prime, nand_404_out);
  nand nand_411 (nand_411_out, nand_405_out, nand_405_out);
  nand nand_412 (nand_412_out, nand_407_out, nand_413_out);
  nand nand_413 (nand_413_out, nand_412_out, nand_408_out);
  nand nand_414 (nand_414_out, nand_405_out, Clk_2);
  nand nand_415 (nand_415_out, Clk_2, nand_411_out);
  nand nand_416 (nand_416_out, nand_412_out, nand_412_out);
  nand nand_417 (Q_5, nand_414_out, PRE_prime_2, Q_prime_5);
  nand nand_418 (Q_prime_5, Q_5, CLR_prime_2, nand_415_out);
  nand nand_419 (nand_419_out, nand_412_out, Clk_3);
  nand nand_420 (nand_420_out, Clk_3, nand_416_out);
  nand nand_421 (Q_6, nand_419_out, PRE_prime_3, Q_prime_6);
  nand nand_422 (Q_prime_6, Q_6, CLR_prime_3, nand_420_out);
  // AND_Gate and_1 is placed but not wired
  // AND_Gate and_2 is placed but not wired

  // Notes on the sheet:
  //   NOT Gate
  //   NAND Gate
  //   AND Gate
  //   OR Gate
  //   NOR Gate
  //   XOR Gate
  //   XNOR Gate
  //   3-input NAND
  //   Full Adder
  //   Half Adder
  //   A
  //   B
  //   A
  //   B
  //   Half Adder
  //   Full Adder
  //   A
  //   B
  //   A
  //   B
  //   2:1 MUX
  //   4:1 MUX
  //   1:2 DEMUX
  //   1:4 DEMUX
  //   4:2 PRIORITY ENCODER
  //   2:4 DECODER
  //   1:2 DEMUX
  //   2:1 MUX
  //   4:1 MUX
  //   4:2 PRIORITY ENCODER
  //   2:4 DECODER
  //   1:4 DEMUX
  //   1-BIT COMPARATOR
  //   4-bit comparator
  //   1-BIT COMPARATOR
  //   E
  //   I0
  //   E
  //   S0
  //   I0
  //   S0
  //   I0
  //   S0
  //   I0
  //   S0
  //   O0
  //   O1
  //   O0
  //   O1
  //   O0
  //   O1
  //   O0
  //   O1
  //   SR Latch
  //   Gated SR Latch
  //   (Gated) D Latch
  //   D Flip Flop
  //   T Flip Flop
  //   JK Flip Flop
  //   D
  //   D
  //   D
endmodule

module HalfAdder (
  input  A,
  input  B,
  output S,
  output C
);

  wire nand_1_out, nand_2_out, nand_3_out, nand_4_out, nand_5_out;

  nand nand_1 (nand_1_out, A, A);
  nand nand_2 (nand_2_out, B, B);
  nand nand_3 (nand_3_out, A, B);
  nand nand_4 (nand_4_out, A, nand_2_out);
  nand nand_5 (nand_5_out, nand_1_out, B);
  nand nand_6 (C, nand_3_out, nand_3_out);
  nand nand_7 (S, nand_4_out, nand_5_out);
endmodule

module FullAdder (
  input  A,
  input  B,
  input  Cin,
  output Sum,
  output Carry
);

  wire nand_1_out, nand_2_out, nand_3_out, nand_4_out, nand_5_out, nand_6_out, nand_7_out, nand_8_out,
       nand_9_out, nand_10_out, nand_11_out, nand_12_out, nand_13_out, nand_14_out, nand_15_out, nand_16_out,
       nand_17_out, nand_18_out;

  nand nand_1 (nand_1_out, A, A);
  nand nand_2 (nand_2_out, B, B);
  nand nand_3 (nand_3_out, A, B);
  nand nand_4 (nand_4_out, A, A);
  nand nand_5 (nand_5_out, B, B);
  nand nand_6 (nand_6_out, A, nand_2_out);
  nand nand_7 (nand_7_out, nand_1_out, B);
  nand nand_8 (nand_8_out, nand_3_out, nand_3_out);
  nand nand_9 (nand_9_out, nand_4_out, nand_5_out);
  nand nand_10 (nand_10_out, nand_6_out, nand_7_out);
  nand nand_11 (nand_11_out, nand_9_out, Cin);
  nand nand_12 (nand_12_out, nand_11_out, nand_11_out);
  nand nand_13 (nand_13_out, nand_10_out, nand_10_out);
  nand nand_14 (nand_14_out, Cin, Cin);
  nand nand_15 (nand_15_out, nand_10_out, nand_14_out);
  nand nand_16 (nand_16_out, nand_13_out, Cin);
  nand nand_17 (nand_17_out, nand_8_out, nand_8_out);
  nand nand_18 (nand_18_out, nand_12_out, nand_12_out);
  nand nand_19 (Sum, nand_15_out, nand_16_out);
  nand nand_20 (Carry, nand_17_out, nand_18_out);

  // Notes on the sheet:
  //   Full Adder
  //   Full Adder
endmodule

module _4bitRippleAdder (
  input  Cin,
  input  A0,
  input  A1,
  input  A2,
  input  A3,
  input  B0,
  input  B1,
  input  B2,
  input  B3,
  output S0,
  output S1,
  output S2,
  output S3,
  output Cout
);

  wire nand_1_out, nand_2_out, nand_3_out, nand_4_out, nand_5_out, nand_6_out, nand_7_out, nand_8_out,
       nand_9_out, nand_10_out, nand_11_out, nand_12_out, nand_13_out, nand_14_out, nand_15_out, nand_16_out,
       nand_17_out, nand_18_out, nand_19_out, nand_20_out, nand_21_out, nand_22_out, nand_23_out,
       nand_24_out, nand_25_out, nand_26_out, nand_27_out, nand_28_out, nand_29_out, nand_30_out,
       nand_31_out, nand_32_out, nand_33_out, nand_34_out, nand_35_out, nand_36_out, nand_38_out,
       nand_40_out, nand_41_out, nand_42_out, nand_43_out, nand_44_out, nand_45_out, nand_46_out,
       nand_47_out, nand_48_out, nand_49_out, nand_50_out, nand_51_out, nand_52_out, nand_53_out,
       nand_54_out, nand_55_out, nand_56_out, nand_57_out, nand_58_out, nand_59_out, nand_60_out,
       nand_61_out, nand_62_out, nand_63_out, nand_64_out, nand_65_out, nand_66_out, nand_67_out,
       nand_68_out, nand_69_out, nand_70_out, nand_71_out, nand_72_out, nand_73_out, nand_74_out,
       nand_75_out, nand_76_out, nand_78_out;

  nand nand_1 (nand_1_out, A0, A0);
  nand nand_2 (nand_2_out, B0, B0);
  nand nand_3 (nand_3_out, A0, B0);
  nand nand_4 (nand_4_out, A0, A0);
  nand nand_5 (nand_5_out, B0, B0);
  nand nand_6 (nand_6_out, A2, A2);
  nand nand_7 (nand_7_out, B2, B2);
  nand nand_8 (nand_8_out, A2, B2);
  nand nand_9 (nand_9_out, A2, A2);
  nand nand_10 (nand_10_out, B2, B2);
  nand nand_11 (nand_11_out, A0, nand_2_out);
  nand nand_12 (nand_12_out, nand_1_out, B0);
  nand nand_13 (nand_13_out, nand_3_out, nand_3_out);
  nand nand_14 (nand_14_out, nand_4_out, nand_5_out);
  nand nand_15 (nand_15_out, A2, nand_7_out);
  nand nand_16 (nand_16_out, nand_6_out, B2);
  nand nand_17 (nand_17_out, nand_8_out, nand_8_out);
  nand nand_18 (nand_18_out, nand_9_out, nand_10_out);
  nand nand_19 (nand_19_out, nand_14_out, Cin);
  nand nand_20 (nand_20_out, nand_15_out, nand_16_out);
  nand nand_21 (nand_21_out, nand_18_out, nand_78_out);
  nand nand_22 (nand_22_out, nand_11_out, nand_12_out);
  nand nand_23 (nand_23_out, nand_19_out, nand_19_out);
  nand nand_24 (nand_24_out, nand_21_out, nand_21_out);
  nand nand_25 (nand_25_out, nand_22_out, nand_22_out);
  nand nand_26 (nand_26_out, Cin, Cin);
  nand nand_27 (nand_27_out, nand_20_out, nand_20_out);
  nand nand_28 (nand_28_out, nand_78_out, nand_78_out);
  nand nand_29 (nand_29_out, nand_22_out, nand_26_out);
  nand nand_30 (nand_30_out, nand_25_out, Cin);
  nand nand_31 (nand_31_out, nand_13_out, nand_13_out);
  nand nand_32 (nand_32_out, nand_23_out, nand_23_out);
  nand nand_33 (nand_33_out, nand_20_out, nand_28_out);
  nand nand_34 (nand_34_out, nand_27_out, nand_78_out);
  nand nand_35 (nand_35_out, nand_17_out, nand_17_out);
  nand nand_36 (nand_36_out, nand_24_out, nand_24_out);
  nand nand_37 (S0, nand_29_out, nand_30_out);
  nand nand_38 (nand_38_out, nand_31_out, nand_32_out);
  nand nand_39 (S2, nand_33_out, nand_34_out);
  nand nand_40 (nand_40_out, nand_35_out, nand_36_out);
  nand nand_41 (nand_41_out, A1, A1);
  nand nand_42 (nand_42_out, B1, B1);
  nand nand_43 (nand_43_out, A1, B1);
  nand nand_44 (nand_44_out, A1, A1);
  nand nand_45 (nand_45_out, B1, B1);
  nand nand_46 (nand_46_out, A3, A3);
  nand nand_47 (nand_47_out, B3, B3);
  nand nand_48 (nand_48_out, A3, B3);
  nand nand_49 (nand_49_out, A3, A3);
  nand nand_50 (nand_50_out, B3, B3);
  nand nand_51 (nand_51_out, A1, nand_42_out);
  nand nand_52 (nand_52_out, nand_41_out, B1);
  nand nand_53 (nand_53_out, nand_43_out, nand_43_out);
  nand nand_54 (nand_54_out, nand_44_out, nand_45_out);
  nand nand_55 (nand_55_out, A3, nand_47_out);
  nand nand_56 (nand_56_out, nand_46_out, B3);
  nand nand_57 (nand_57_out, nand_48_out, nand_48_out);
  nand nand_58 (nand_58_out, nand_49_out, nand_50_out);
  nand nand_59 (nand_59_out, nand_54_out, nand_38_out);
  nand nand_60 (nand_60_out, nand_55_out, nand_56_out);
  nand nand_61 (nand_61_out, nand_58_out, nand_40_out);
  nand nand_62 (nand_62_out, nand_51_out, nand_52_out);
  nand nand_63 (nand_63_out, nand_59_out, nand_59_out);
  nand nand_64 (nand_64_out, nand_61_out, nand_61_out);
  nand nand_65 (nand_65_out, nand_62_out, nand_62_out);
  nand nand_66 (nand_66_out, nand_38_out, nand_38_out);
  nand nand_67 (nand_67_out, nand_60_out, nand_60_out);
  nand nand_68 (nand_68_out, nand_40_out, nand_40_out);
  nand nand_69 (nand_69_out, nand_62_out, nand_66_out);
  nand nand_70 (nand_70_out, nand_65_out, nand_38_out);
  nand nand_71 (nand_71_out, nand_53_out, nand_53_out);
  nand nand_72 (nand_72_out, nand_63_out, nand_63_out);
  nand nand_73 (nand_73_out, nand_60_out, nand_68_out);
  nand nand_74 (nand_74_out, nand_67_out, nand_40_out);
  nand nand_75 (nand_75_out, nand_57_out, nand_57_out);
  nand nand_76 (nand_76_out, nand_64_out, nand_64_out);
  nand nand_77 (S1, nand_69_out, nand_70_out);
  nand nand_78 (nand_78_out, nand_71_out, nand_72_out);
  nand nand_79 (S3, nand_73_out, nand_74_out);
  nand nand_80 (Cout, nand_75_out, nand_76_out);

  // Notes on the sheet:
  //   A
  //   B
  //   A
  //   B
  //   A
  //   B
  //   A
  //   B
endmodule

module _2_1MUX (
  input  I0,
  input  I1,
  input  S0,
  output Output
);

  wire nand_1_out, nand_2_out, nand_3_out;

  nand nand_1 (nand_1_out, S0, S0);
  nand nand_2 (nand_2_out, I0, nand_1_out);
  nand nand_3 (nand_3_out, I1, S0);
  nand nand_4 (Output, nand_2_out, nand_3_out);

  // Notes on the sheet:
  //   2:1 MUX
  //   2:1 MUX
endmodule

module _4_1MUX (
  input  I0,
  input  I1,
  input  I2,
  input  I3,
  input  S0,
  input  S1,
  output Output
);

  wire nand_1_out, nand_2_out, nand_3_out, nand_4_out, nand_5_out, nand_6_out, nand_7_out, nand_8_out,
       nand_9_out, nand_10_out, nand_11_out;

  nand nand_1 (nand_1_out, S0, S0);
  nand nand_2 (nand_2_out, S0, S0);
  nand nand_3 (nand_3_out, I0, nand_1_out);
  nand nand_4 (nand_4_out, I1, S0);
  nand nand_5 (nand_5_out, I2, nand_2_out);
  nand nand_6 (nand_6_out, I3, S0);
  nand nand_7 (nand_7_out, nand_3_out, nand_4_out);
  nand nand_8 (nand_8_out, nand_5_out, nand_6_out);
  nand nand_9 (nand_9_out, S1, S1);
  nand nand_10 (nand_10_out, nand_7_out, nand_9_out);
  nand nand_11 (nand_11_out, nand_8_out, S1);
  nand nand_12 (Output, nand_10_out, nand_11_out);

  // Notes on the sheet:
  //   4:1 MUX
  //   4:1 MUX
endmodule

module _1_2DEMUX (
  input  I0,
  input  O0,
  output O0_2,
  output O1
);

  wire nand_1_out, nand_2_out, nand_3_out;

  nand nand_1 (nand_1_out, O0, O0);
  nand nand_2 (nand_2_out, I0, nand_1_out);
  nand nand_3 (nand_3_out, I0, O0);
  nand nand_4 (O0_2, nand_2_out, nand_2_out);
  nand nand_5 (O1, nand_3_out, nand_3_out);

  // Notes on the sheet:
  //   1:2 DEMUX
  //   1:2 DEMUX
endmodule

module _1_4DEMUX (
  input  I0,
  input  S0,
  input  S1,
  output O0,
  output O1,
  output O2,
  output O3
);

  wire nand_1_out, nand_2_out, nand_3_out, nand_4_out, nand_5_out, nand_6_out, nand_7_out, nand_8_out,
       nand_9_out, nand_10_out, nand_11_out;

  nand nand_1 (nand_1_out, S1, S1);
  nand nand_2 (nand_2_out, I0, nand_1_out);
  nand nand_3 (nand_3_out, I0, S1);
  nand nand_4 (nand_4_out, nand_2_out, nand_2_out);
  nand nand_5 (nand_5_out, nand_3_out, nand_3_out);
  nand nand_6 (nand_6_out, S0, S0);
  nand nand_7 (nand_7_out, S0, S0);
  nand nand_8 (nand_8_out, nand_4_out, nand_6_out);
  nand nand_9 (nand_9_out, nand_4_out, S0);
  nand nand_10 (nand_10_out, nand_5_out, nand_7_out);
  nand nand_11 (nand_11_out, nand_5_out, S0);
  nand nand_12 (O0, nand_8_out, nand_8_out);
  nand nand_13 (O1, nand_9_out, nand_9_out);
  nand nand_14 (O2, nand_10_out, nand_10_out);
  nand nand_15 (O3, nand_11_out, nand_11_out);

  // Notes on the sheet:
  //   1:4 DEMUX
  //   1:4 DEMUX
endmodule

module _4_2PriorityEncoder (
  input  I3,
  input  I2,
  input  I1,
  input  I0,
  output O0,
  output O1,
  output Valid
);

  wire nand_1_out, nand_2_out, nand_3_out, nand_4_out, nand_5_out, nand_6_out, nand_7_out, nand_8_out,
       nand_9_out, nand_10_out, nand_11_out, nand_12_out, nand_13_out, nand_14_out, nand_15_out;

  nand nand_1 (nand_1_out, I2, I2);
  nand nand_2 (nand_2_out, I3, I3);
  nand nand_3 (nand_3_out, I2, I2);
  nand nand_4 (nand_4_out, I1, I1);
  nand nand_5 (nand_5_out, I0, I0);
  nand nand_6 (nand_6_out, I1, nand_1_out);
  nand nand_7 (nand_7_out, nand_2_out, nand_3_out);
  nand nand_8 (nand_8_out, nand_4_out, nand_5_out);
  nand nand_9 (nand_9_out, nand_6_out, nand_6_out);
  nand nand_10 (nand_10_out, nand_9_out, nand_9_out);
  nand nand_11 (nand_11_out, I3, I3);
  nand nand_12 (nand_12_out, I2, I2);
  nand nand_13 (nand_13_out, I3, I3);
  nand nand_14 (nand_14_out, nand_7_out, nand_7_out);
  nand nand_15 (nand_15_out, nand_8_out, nand_8_out);
  nand nand_16 (O0, nand_10_out, nand_11_out);
  nand nand_17 (O1, nand_12_out, nand_13_out);
  nand nand_18 (Valid, nand_14_out, nand_15_out);

  // Notes on the sheet:
  //   4:2 PRIORITY ENCODER
  //   4:2 PRIORITY ENCODER
endmodule

module _2_4Decoder (
  input  I0,
  input  I1,
  output O0,
  output O1,
  output O2,
  output O3
);

  wire nand_1_out, nand_2_out, nand_3_out, nand_4_out, nand_5_out, nand_6_out;

  nand nand_1 (nand_1_out, I0, I0);
  nand nand_2 (nand_2_out, I1, I1);
  nand nand_3 (nand_3_out, nand_1_out, nand_2_out);
  nand nand_4 (nand_4_out, I0, nand_2_out);
  nand nand_5 (nand_5_out, nand_1_out, I1);
  nand nand_6 (nand_6_out, I0, I1);
  nand nand_7 (O0, nand_3_out, nand_3_out);
  nand nand_8 (O1, nand_4_out, nand_4_out);
  nand nand_9 (O2, nand_5_out, nand_5_out);
  nand nand_10 (O3, nand_6_out, nand_6_out);

  // Notes on the sheet:
  //   2:4 DECODER
  //   2:4 DECODER
endmodule

module _1_bitComparator (
  input  A,
  input  B,
  output L_A_B,
  output E,
  output G_A_B
);

  wire nand_1_out, nand_2_out, nand_3_out, nand_4_out, nand_5_out, nand_6_out, nand_7_out, nand_8_out,
       nand_9_out;

  nand nand_1 (nand_1_out, A, A);
  nand nand_2 (nand_2_out, B, B);
  nand nand_3 (nand_3_out, A, A);
  nand nand_4 (nand_4_out, A, nand_2_out);
  nand nand_5 (nand_5_out, nand_1_out, B);
  nand nand_6 (nand_6_out, B, B);
  nand nand_7 (nand_7_out, nand_3_out, A);
  nand nand_8 (nand_8_out, nand_4_out, nand_5_out);
  nand nand_9 (nand_9_out, B, nand_6_out);
  nand nand_10 (L_A_B, nand_7_out, nand_7_out);
  nand nand_11 (E, nand_8_out, nand_8_out);
  nand nand_12 (G_A_B, nand_9_out, nand_9_out);

  // Notes on the sheet:
  //   1-BIT COMPARATOR
endmodule

module _4_bitComparator (
  input  A3,
  input  A2,
  input  A1,
  input  A0,
  input  B3,
  input  B2,
  input  B1,
  input  B0,
  input  LOGIC1,
  output L_A_B,
  output E,
  output G_A_B
);

  wire nand_1_out, nand_2_out, nand_3_out, nand_4_out, nand_5_out, nand_6_out, nand_7_out, nand_8_out,
       nand_9_out, nand_10_out, nand_11_out, nand_12_out, nand_13_out, nand_14_out, nand_15_out, nand_16_out,
       nand_17_out, nand_18_out, nand_19_out, nand_20_out, nand_21_out, nand_22_out, nand_23_out,
       nand_24_out, nand_25_out, nand_26_out, nand_27_out, nand_28_out, nand_29_out, nand_30_out,
       nand_31_out, nand_32_out, nand_33_out, nand_34_out, nand_35_out, nand_36_out, nand_37_out,
       nand_38_out, nand_39_out, nand_40_out, nand_41_out, nand_42_out, nand_43_out, nand_44_out,
       nand_45_out, nand_46_out, nand_47_out, nand_48_out, nand_49_out, nand_50_out, nand_51_out,
       nand_52_out, nand_53_out, nand_54_out, nand_55_out, nand_56_out, nand_57_out, nand_58_out,
       nand_59_out, nand_60_out, nand_61_out, nand_62_out, nand_63_out, nand_64_out, nand_65_out,
       nand_66_out, nand_67_out, nand_68_out, nand_69_out, nand_70_out, nand_71_out, nand_72_out,
       nand_73_out, nand_74_out, nand_75_out, nand_76_out, nand_77_out, nand_78_out, nand_79_out,
       nand_81_out, nand_82_out, nand_83_out, nand_84_out, nand_85_out, nand_86_out, nand_87_out,
       nand_88_out, nand_89_out, nand_90_out, nand_91_out, nand_92_out, nand_93_out, nand_94_out,
       nand_95_out, nand_96_out, nand_97_out, nand_98_out, nand_99_out, nand_100_out, nand_101_out,
       nand_102_out, nand_103_out, nand_104_out, nand_105_out, nand_106_out, nand_107_out, nand_108_out,
       nand_109_out, nand_110_out, nand_111_out, nand_112_out, nand_113_out, nand_114_out, nand_115_out,
       nand_116_out, nand_117_out, nand_118_out;

  nand nand_1 (nand_1_out, A3, A3);
  nand nand_2 (nand_2_out, B3, B3);
  nand nand_3 (nand_3_out, A2, A2);
  nand nand_4 (nand_4_out, B2, B2);
  nand nand_5 (nand_5_out, A1, A1);
  nand nand_6 (nand_6_out, B1, B1);
  nand nand_7 (nand_7_out, A0, A0);
  nand nand_8 (nand_8_out, B0, B0);
  nand nand_9 (nand_9_out, A3, A3);
  nand nand_10 (nand_10_out, A3, nand_2_out);
  nand nand_11 (nand_11_out, nand_1_out, B3);
  nand nand_12 (nand_12_out, B3, B3);
  nand nand_13 (nand_13_out, A2, A2);
  nand nand_14 (nand_14_out, A2, nand_4_out);
  nand nand_15 (nand_15_out, nand_3_out, B2);
  nand nand_16 (nand_16_out, B2, B2);
  nand nand_17 (nand_17_out, A1, A1);
  nand nand_18 (nand_18_out, A1, nand_6_out);
  nand nand_19 (nand_19_out, nand_5_out, B1);
  nand nand_20 (nand_20_out, B1, B1);
  nand nand_21 (nand_21_out, A0, A0);
  nand nand_22 (nand_22_out, A0, nand_8_out);
  nand nand_23 (nand_23_out, nand_7_out, B0);
  nand nand_24 (nand_24_out, B0, B0);
  nand nand_25 (nand_25_out, nand_9_out, A3);
  nand nand_26 (nand_26_out, nand_10_out, nand_11_out);
  nand nand_27 (nand_27_out, B3, nand_12_out);
  nand nand_28 (nand_28_out, nand_13_out, A2);
  nand nand_29 (nand_29_out, nand_14_out, nand_15_out);
  nand nand_30 (nand_30_out, B2, nand_16_out);
  nand nand_31 (nand_31_out, nand_17_out, A1);
  nand nand_32 (nand_32_out, nand_18_out, nand_19_out);
  nand nand_33 (nand_33_out, B1, nand_20_out);
  nand nand_34 (nand_34_out, nand_21_out, A0);
  nand nand_35 (nand_35_out, nand_22_out, nand_23_out);
  nand nand_36 (nand_36_out, B0, nand_24_out);
  nand nand_37 (nand_37_out, nand_25_out, nand_25_out);
  nand nand_38 (nand_38_out, nand_26_out, nand_26_out);
  nand nand_39 (nand_39_out, nand_27_out, nand_27_out);
  nand nand_40 (nand_40_out, nand_28_out, nand_28_out);
  nand nand_41 (nand_41_out, nand_29_out, nand_29_out);
  nand nand_42 (nand_42_out, nand_30_out, nand_30_out);
  nand nand_43 (nand_43_out, nand_31_out, nand_31_out);
  nand nand_44 (nand_44_out, nand_32_out, nand_32_out);
  nand nand_45 (nand_45_out, nand_33_out, nand_33_out);
  nand nand_46 (nand_46_out, nand_34_out, nand_34_out);
  nand nand_47 (nand_47_out, nand_35_out, nand_35_out);
  nand nand_48 (nand_48_out, nand_36_out, nand_36_out);
  nand nand_49 (nand_49_out, nand_38_out, nand_38_out);
  nand nand_50 (nand_50_out, nand_41_out, nand_41_out);
  nand nand_51 (nand_51_out, nand_44_out, nand_44_out);
  nand nand_52 (nand_52_out, nand_47_out, nand_47_out);
  nand nand_53 (nand_53_out, LOGIC1, nand_49_out);
  nand nand_54 (nand_54_out, LOGIC1, nand_38_out);
  nand nand_55 (nand_55_out, LOGIC1, nand_50_out);
  nand nand_56 (nand_56_out, LOGIC1, nand_41_out);
  nand nand_57 (nand_57_out, LOGIC1, nand_51_out);
  nand nand_58 (nand_58_out, LOGIC1, nand_44_out);
  nand nand_59 (nand_59_out, LOGIC1, nand_52_out);
  nand nand_60 (nand_60_out, LOGIC1, nand_47_out);
  nand nand_61 (nand_61_out, nand_53_out, nand_53_out);
  nand nand_62 (nand_62_out, nand_54_out, nand_54_out);
  nand nand_63 (nand_63_out, nand_55_out, nand_55_out);
  nand nand_64 (nand_64_out, nand_56_out, nand_56_out);
  nand nand_65 (nand_65_out, nand_57_out, nand_57_out);
  nand nand_66 (nand_66_out, nand_58_out, nand_58_out);
  nand nand_67 (nand_67_out, nand_59_out, nand_59_out);
  nand nand_68 (nand_68_out, nand_60_out, nand_60_out);
  nand nand_69 (nand_69_out, nand_62_out, nand_63_out);
  nand nand_70 (nand_70_out, nand_62_out, nand_64_out);
  nand nand_71 (nand_71_out, nand_76_out, nand_65_out);
  nand nand_72 (nand_72_out, nand_76_out, nand_66_out);
  nand nand_73 (nand_73_out, nand_78_out, nand_67_out);
  nand nand_74 (nand_74_out, nand_78_out, nand_68_out);
  nand nand_75 (nand_75_out, nand_69_out, nand_69_out);
  nand nand_76 (nand_76_out, nand_70_out, nand_70_out);
  nand nand_77 (nand_77_out, nand_71_out, nand_71_out);
  nand nand_78 (nand_78_out, nand_72_out, nand_72_out);
  nand nand_79 (nand_79_out, nand_73_out, nand_73_out);
  nand nand_80 (E, nand_74_out, nand_74_out);
  nand nand_81 (nand_81_out, nand_37_out, nand_37_out);
  nand nand_82 (nand_82_out, nand_40_out, nand_40_out);
  nand nand_83 (nand_83_out, nand_43_out, nand_43_out);
  nand nand_84 (nand_84_out, nand_46_out, nand_46_out);
  nand nand_85 (nand_85_out, nand_61_out, nand_61_out);
  nand nand_86 (nand_86_out, nand_75_out, nand_75_out);
  nand nand_87 (nand_87_out, nand_77_out, nand_77_out);
  nand nand_88 (nand_88_out, nand_79_out, nand_79_out);
  nand nand_89 (nand_89_out, nand_39_out, nand_39_out);
  nand nand_90 (nand_90_out, nand_42_out, nand_42_out);
  nand nand_91 (nand_91_out, nand_45_out, nand_45_out);
  nand nand_92 (nand_92_out, nand_48_out, nand_48_out);
  nand nand_93 (nand_93_out, nand_61_out, nand_61_out);
  nand nand_94 (nand_94_out, nand_75_out, nand_75_out);
  nand nand_95 (nand_95_out, nand_77_out, nand_77_out);
  nand nand_96 (nand_96_out, nand_79_out, nand_79_out);
  nand nand_97 (nand_97_out, nand_81_out, nand_82_out);
  nand nand_98 (nand_98_out, nand_83_out, nand_84_out);
  nand nand_99 (nand_99_out, nand_85_out, nand_86_out);
  nand nand_100 (nand_100_out, nand_87_out, nand_88_out);
  nand nand_101 (nand_101_out, nand_89_out, nand_90_out);
  nand nand_102 (nand_102_out, nand_91_out, nand_92_out);
  nand nand_103 (nand_103_out, nand_93_out, nand_94_out);
  nand nand_104 (nand_104_out, nand_95_out, nand_96_out);
  nand nand_105 (nand_105_out, nand_97_out, nand_97_out);
  nand nand_106 (nand_106_out, nand_98_out, nand_98_out);
  nand nand_107 (nand_107_out, nand_99_out, nand_99_out);
  nand nand_108 (nand_108_out, nand_100_out, nand_100_out);
  nand nand_109 (nand_109_out, nand_101_out, nand_101_out);
  nand nand_110 (nand_110_out, nand_102_out, nand_102_out);
  nand nand_111 (nand_111_out, nand_103_out, nand_103_out);
  nand nand_112 (nand_112_out, nand_104_out, nand_104_out);
  nand nand_113 (nand_113_out, nand_105_out, nand_106_out);
  nand nand_114 (nand_114_out, nand_107_out, nand_108_out);
  nand nand_115 (nand_115_out, nand_109_out, nand_110_out);
  nand nand_116 (nand_116_out, nand_111_out, nand_112_out);
  nand nand_117 (nand_117_out, nand_113_out, nand_114_out);
  nand nand_118 (nand_118_out, nand_115_out, nand_116_out);
  nand nand_119 (L_A_B, nand_117_out, nand_117_out);
  nand nand_120 (G_A_B, nand_118_out, nand_118_out);

  // Notes on the sheet:
  //   4-bit comparator
  //   I0
  //   E
  //   S0
  //   I0
  //   E
  //   S0
  //   I0
  //   S0
  //   I0
  //   S0
  //   O0
  //   O1
  //   O0
  //   O1
  //   O0
  //   O1
  //   O0
  //   O1
endmodule

module SRLatch (
  input  S_prime,
  input  R_prime,
  output Q,
  output Q_prime
);

  nand nand_1 (Q, S_prime, Q_prime);
  nand nand_2 (Q_prime, Q, R_prime);

  // Notes on the sheet:
  //   SR Latch
endmodule

module GatedSRLatch (
  input  S,
  input  EN,
  input  R,
  output Q,
  output Q_prime
);

  wire nand_1_out, nand_2_out;

  nand nand_1 (nand_1_out, S, EN);
  nand nand_2 (nand_2_out, EN, R);
  nand nand_3 (Q, nand_1_out, Q_prime);
  nand nand_4 (Q_prime, Q, nand_2_out);

  // Notes on the sheet:
  //   Gated SR Latch
endmodule

module DLatch (
  input  D,
  input  EN,
  output Q,
  output Q_prime
);

  wire nand_1_out, nand_2_out, nand_3_out;

  nand nand_1 (nand_1_out, D, D);
  nand nand_2 (nand_2_out, D, EN);
  nand nand_3 (nand_3_out, EN, nand_1_out);
  nand nand_4 (Q, nand_2_out, Q_prime);
  nand nand_5 (Q_prime, Q, nand_3_out);
endmodule

module DFlipFlop (
  input  PRE_prime,
  input  D,
  input  Clk,
  input  CLR_prime,
  output Q,
  output Q_prime
);

  wire nand_1_out, nand_2_out, nand_3_out, nand_4_out, nand_5_out, nand_6_out, nand_7_out, nand_8_out,
       nand_9_out;

  nand nand_1 (nand_1_out, D, D);
  nand nand_2 (nand_2_out, Clk, Clk);
  nand nand_3 (nand_3_out, D, nand_2_out);
  nand nand_4 (nand_4_out, nand_2_out, nand_1_out);
  nand nand_5 (nand_5_out, nand_3_out, nand_6_out);
  nand nand_6 (nand_6_out, nand_5_out, nand_4_out);
  nand nand_7 (nand_7_out, nand_5_out, nand_5_out);
  nand nand_8 (nand_8_out, nand_5_out, Clk);
  nand nand_9 (nand_9_out, Clk, nand_7_out);
  nand nand_10 (Q, nand_8_out, PRE_prime, Q_prime);
  nand nand_11 (Q_prime, Q, CLR_prime, nand_9_out);

  // Notes on the sheet:
  //   D
endmodule

module TFlipFlop (
  input  PRE_prime,
  input  T,
  input  Clk,
  input  CLR_prime,
  output Q,
  output Q_prime
);

  wire nand_1_out, nand_2_out, nand_3_out, nand_4_out, nand_5_out, nand_6_out, nand_7_out, nand_8_out,
       nand_9_out, nand_10_out, nand_11_out, nand_12_out, nand_13_out, nand_14_out;

  nand nand_1 (nand_1_out, Q, Q);
  nand nand_2 (nand_2_out, T, T);
  nand nand_3 (nand_3_out, Q, nand_2_out);
  nand nand_4 (nand_4_out, nand_1_out, T);
  nand nand_5 (nand_5_out, nand_3_out, nand_4_out);
  nand nand_6 (nand_6_out, nand_5_out, nand_5_out);
  nand nand_7 (nand_7_out, Clk, Clk);
  nand nand_8 (nand_8_out, nand_5_out, nand_7_out);
  nand nand_9 (nand_9_out, nand_7_out, nand_6_out);
  nand nand_10 (nand_10_out, nand_8_out, nand_11_out);
  nand nand_11 (nand_11_out, nand_10_out, nand_9_out);
  nand nand_12 (nand_12_out, nand_10_out, nand_10_out);
  nand nand_13 (nand_13_out, nand_10_out, Clk);
  nand nand_14 (nand_14_out, Clk, nand_12_out);
  nand nand_15 (Q, nand_13_out, PRE_prime, Q_prime);
  nand nand_16 (Q_prime, Q, CLR_prime, nand_14_out);

  // Notes on the sheet:
  //   D
endmodule

module JKFlipFlop (
  input  PRE_prime,
  input  J,
  input  K,
  input  Clk,
  input  CLR_prime,
  output Q,
  output Q_prime
);

  wire nand_1_out, nand_2_out, nand_3_out, nand_4_out, nand_5_out, nand_6_out, nand_7_out, nand_8_out,
       nand_9_out, nand_10_out, nand_11_out, nand_12_out, nand_13_out;

  nand nand_1 (nand_1_out, K, K);
  nand nand_2 (nand_2_out, Q_prime, J);
  nand nand_3 (nand_3_out, Q, nand_1_out);
  nand nand_4 (nand_4_out, nand_2_out, nand_3_out);
  nand nand_5 (nand_5_out, nand_4_out, nand_4_out);
  nand nand_6 (nand_6_out, Clk, Clk);
  nand nand_7 (nand_7_out, nand_4_out, nand_6_out);
  nand nand_8 (nand_8_out, nand_7_out, nand_9_out);
  nand nand_9 (nand_9_out, nand_8_out, nand_10_out);
  nand nand_10 (nand_10_out, nand_6_out, nand_5_out);
  nand nand_11 (nand_11_out, nand_8_out, nand_8_out);
  nand nand_12 (nand_12_out, nand_8_out, Clk);
  nand nand_13 (nand_13_out, Clk, nand_11_out);
  nand nand_14 (Q, nand_12_out, PRE_prime, Q_prime);
  nand nand_15 (Q_prime, Q, CLR_prime, nand_13_out);

  // Notes on the sheet:
  //   D
endmodule

module _1bitRegister (
  input  PRE_prime,
  input  DATA,
  input  LOAD,
  input  Clk,
  input  CLR_prime,
  output O
);

  wire n2_1mux_1_output;

  _2_1MUX u_2_1mux_1 (.I0(O), .I1(DATA), .S0(LOAD), .Output(n2_1mux_1_output));
  DFlipFlop dflipflop_1 (
    .D(n2_1mux_1_output), .Clk(Clk), .Q(O), .PRE_prime(PRE_prime), .CLR_prime(CLR_prime));  // open: Q_prime
endmodule

module _4bitRegister (
  input  PRE_prime,
  input  CLR_prime,
  input  Clk,
  input  LOAD,
  input  D0,
  input  D1,
  input  D2,
  input  D3,
  output O,
  output O_2,
  output O_3,
  output O_4
);

  wire n2_1mux_1_output, n2_1mux_2_output, n2_1mux_3_output, n2_1mux_4_output;

  _2_1MUX u_2_1mux_1 (.I0(O), .I1(D0), .S0(LOAD), .Output(n2_1mux_1_output));
  _2_1MUX u_2_1mux_2 (.I0(O_2), .I1(D1), .S0(LOAD), .Output(n2_1mux_2_output));
  _2_1MUX u_2_1mux_3 (.I0(O_3), .I1(D2), .S0(LOAD), .Output(n2_1mux_3_output));
  _2_1MUX u_2_1mux_4 (.I0(O_4), .I1(D3), .S0(LOAD), .Output(n2_1mux_4_output));
  DFlipFlop dflipflop_1 (
    .D(n2_1mux_1_output), .Clk(Clk), .Q(O), .PRE_prime(PRE_prime), .CLR_prime(CLR_prime));  // open: Q_prime
  DFlipFlop dflipflop_2 (
    .D(n2_1mux_2_output), .Clk(Clk), .Q(O_2), .PRE_prime(PRE_prime), .CLR_prime(CLR_prime));  // open: Q_prime
  DFlipFlop dflipflop_3 (
    .D(n2_1mux_3_output), .Clk(Clk), .Q(O_3), .PRE_prime(PRE_prime), .CLR_prime(CLR_prime));  // open: Q_prime
  DFlipFlop dflipflop_4 (
    .D(n2_1mux_4_output), .Clk(Clk), .Q(O_4), .PRE_prime(PRE_prime), .CLR_prime(CLR_prime));  // open: Q_prime
endmodule

module _4bitRegisterWithENandLOAD (
  input  PRE_prime,
  input  CLR_prime,
  input  Clk,
  input  EN,
  input  LOAD,
  input  D0,
  input  D1,
  input  D2,
  input  D3,
  output O,
  output O_2,
  output O_3,
  output O_4
);

  wire n2_1mux_1_output, n2_1mux_2_output, n2_1mux_3_output, n2_1mux_4_output, nand_1_out, nand_2_out;

  nand nand_1 (nand_1_out, Clk, EN);
  nand nand_2 (nand_2_out, nand_1_out, nand_1_out);
  _2_1MUX u_2_1mux_1 (.I0(O), .I1(D0), .S0(LOAD), .Output(n2_1mux_1_output));
  _2_1MUX u_2_1mux_2 (.I0(O_2), .I1(D1), .S0(LOAD), .Output(n2_1mux_2_output));
  _2_1MUX u_2_1mux_3 (.I0(O_3), .I1(D2), .S0(LOAD), .Output(n2_1mux_3_output));
  _2_1MUX u_2_1mux_4 (.I0(O_4), .I1(D3), .S0(LOAD), .Output(n2_1mux_4_output));
  DFlipFlop dflipflop_1 (
    .D(n2_1mux_1_output), .Clk(nand_2_out), .Q(O), .PRE_prime(PRE_prime), .CLR_prime(CLR_prime));  // open: Q_prime
  DFlipFlop dflipflop_2 (
    .D(n2_1mux_2_output), .Clk(nand_2_out), .Q(O_2), .PRE_prime(PRE_prime), .CLR_prime(CLR_prime));  // open: Q_prime
  DFlipFlop dflipflop_3 (
    .D(n2_1mux_3_output), .Clk(nand_2_out), .Q(O_3), .PRE_prime(PRE_prime), .CLR_prime(CLR_prime));  // open: Q_prime
  DFlipFlop dflipflop_4 (
    .D(n2_1mux_4_output), .Clk(nand_2_out), .Q(O_4), .PRE_prime(PRE_prime), .CLR_prime(CLR_prime));  // open: Q_prime
endmodule

module _4bitShiftRegister (
  input  PRE_prime,
  input  I,
  input  Clk,
  input  SHIFT,
  input  CLR_prime,
  output O
);

  wire dflipflop_1_q, dflipflop_2_q, dflipflop_3_q, n2_1mux_1_output, n2_1mux_2_output, n2_1mux_3_output,
       n2_1mux_4_output;

  _2_1MUX u_2_1mux_1 (.I0(dflipflop_1_q), .I1(I), .S0(SHIFT), .Output(n2_1mux_1_output));
  DFlipFlop dflipflop_1 (
    .D(n2_1mux_1_output), .Clk(Clk), .Q(dflipflop_1_q), .PRE_prime(PRE_prime), .CLR_prime(CLR_prime));  // open: Q_prime
  _2_1MUX u_2_1mux_2 (.I0(dflipflop_2_q), .I1(dflipflop_1_q), .S0(SHIFT), .Output(n2_1mux_2_output));
  DFlipFlop dflipflop_2 (
    .D(n2_1mux_2_output), .Clk(Clk), .Q(dflipflop_2_q), .PRE_prime(PRE_prime), .CLR_prime(CLR_prime));  // open: Q_prime
  DFlipFlop dflipflop_3 (
    .D(n2_1mux_3_output), .Clk(Clk), .Q(dflipflop_3_q), .PRE_prime(PRE_prime), .CLR_prime(CLR_prime));  // open: Q_prime
  _2_1MUX u_2_1mux_3 (.I0(dflipflop_3_q), .I1(dflipflop_2_q), .S0(SHIFT), .Output(n2_1mux_3_output));
  _2_1MUX u_2_1mux_4 (.I0(O), .I1(dflipflop_3_q), .S0(SHIFT), .Output(n2_1mux_4_output));
  DFlipFlop dflipflop_4 (
    .D(n2_1mux_4_output), .Clk(Clk), .Q(O), .PRE_prime(PRE_prime), .CLR_prime(CLR_prime));  // open: Q_prime
endmodule

module _4bitBidirectionalShiftRegister (
  input  DIR_1______0,
  input  Lin,
  input  Rin,
  input  PRE_prime,
  input  SHIFT,
  input  Clk,
  input  CLR_prime,
  output Lout,
  output Rout
);

  wire dflipflop_2_q, dflipflop_3_q, n2_1mux_1_output, n2_1mux_2_output, n2_1mux_3_output, n2_1mux_4_output,
       nand_1_out, nand_2_out, nand_3_out, nand_4_out, nand_5_out, nand_6_out, nand_7_out, nand_8_out,
       nand_9_out, nand_10_out, nand_11_out, nand_12_out, nand_13_out;

  nand nand_1 (nand_1_out, DIR_1______0, DIR_1______0);
  nand nand_2 (nand_2_out, Lin, DIR_1______0);
  nand nand_3 (nand_3_out, nand_1_out, dflipflop_2_q);
  nand nand_4 (nand_4_out, nand_2_out, nand_3_out);
  _2_1MUX u_2_1mux_1 (.I0(Lout), .I1(nand_4_out), .S0(SHIFT), .Output(n2_1mux_1_output));
  nand nand_5 (nand_5_out, Lout, DIR_1______0);
  DFlipFlop dflipflop_1 (
    .D(n2_1mux_1_output), .Clk(Clk), .Q(Lout), .PRE_prime(PRE_prime), .CLR_prime(CLR_prime));  // open: Q_prime
  nand nand_6 (nand_6_out, nand_1_out, dflipflop_3_q);
  nand nand_7 (nand_7_out, nand_5_out, nand_6_out);
  _2_1MUX u_2_1mux_2 (.I0(dflipflop_2_q), .I1(nand_7_out), .S0(SHIFT), .Output(n2_1mux_2_output));
  nand nand_8 (nand_8_out, dflipflop_2_q, DIR_1______0);
  DFlipFlop dflipflop_2 (
    .D(n2_1mux_2_output), .Clk(Clk), .Q(dflipflop_2_q), .PRE_prime(PRE_prime), .CLR_prime(CLR_prime));  // open: Q_prime
  nand nand_9 (nand_9_out, nand_1_out, Rout);
  nand nand_10 (nand_10_out, nand_8_out, nand_9_out);
  _2_1MUX u_2_1mux_3 (.I0(dflipflop_3_q), .I1(nand_10_out), .S0(SHIFT), .Output(n2_1mux_3_output));
  nand nand_11 (nand_11_out, dflipflop_3_q, DIR_1______0);
  DFlipFlop dflipflop_3 (
    .D(n2_1mux_3_output), .Clk(Clk), .Q(dflipflop_3_q), .PRE_prime(PRE_prime), .CLR_prime(CLR_prime));  // open: Q_prime
  nand nand_12 (nand_12_out, nand_1_out, Rin);
  nand nand_13 (nand_13_out, nand_11_out, nand_12_out);
  _2_1MUX u_2_1mux_4 (.I0(Rout), .I1(nand_13_out), .S0(SHIFT), .Output(n2_1mux_4_output));
  DFlipFlop dflipflop_4 (
    .D(n2_1mux_4_output), .Clk(Clk), .Q(Rout), .PRE_prime(PRE_prime), .CLR_prime(CLR_prime));  // open: Q_prime
endmodule

module _4bitUniversalRegister (
  input  P3,
  input  P2,
  input  P1,
  input  P0,
  input  DIR_1______0,
  input  Lin,
  input  Rin,
  input  PRE_prime,
  input  INPUT_MODE_1_ParallelIn__0_SerialIn,
  input  SHIFT,
  input  Clk,
  input  CLR_prime,
  input  OUTPUT_MODE_Parallel_1__Serial_0,
  output Lout,
  output Rout,
  output O3,
  output O2,
  output O1,
  output O0
);

  wire dflipflop_1_q, dflipflop_2_q, dflipflop_3_q, dflipflop_4_q, n2_1mux_1_output, n2_1mux_2_output,
       n2_1mux_3_output, n2_1mux_4_output, n2_1mux_5_output, n2_1mux_7_output, n2_1mux_8_output, nand_1_out,
       nand_2_out, nand_3_out, nand_4_out, nand_5_out, nand_7_out, nand_8_out, nand_10_out, nand_11_out,
       nand_12_out, nand_13_out, nand_14_out, nand_16_out, nand_17_out, nand_19_out, nand_20_out,
       nand_21_out, nand_22_out, nand_24_out, nand_25_out;

  nand nand_1 (nand_1_out, DIR_1______0, DIR_1______0);
  nand nand_2 (nand_2_out, Lin, DIR_1______0);
  nand nand_3 (nand_3_out, nand_1_out, PRE_prime);
  nand nand_4 (nand_4_out, nand_2_out, nand_3_out);
  nand nand_5 (nand_5_out, nand_24_out, dflipflop_1_q);
  _2_1MUX u_2_1mux_1 (.I0(dflipflop_1_q), .I1(nand_4_out), .S0(SHIFT), .Output(n2_1mux_1_output));
  _2_1MUX u_2_1mux_2 (
    .I0(n2_1mux_1_output), .I1(P3), .S0(INPUT_MODE_1_ParallelIn__0_SerialIn), .Output(n2_1mux_2_output));
  nand nand_6 (Lout, nand_5_out, nand_5_out);
  nand nand_7 (nand_7_out, dflipflop_1_q, DIR_1______0);
  DFlipFlop dflipflop_1 (
    .D(n2_1mux_2_output), .Clk(Clk), .Q(dflipflop_1_q), .PRE_prime(PRE_prime), .CLR_prime(CLR_prime));  // open: Q_prime
  nand nand_8 (nand_8_out, OUTPUT_MODE_Parallel_1__Serial_0, dflipflop_1_q);
  nand nand_9 (O3, nand_8_out, nand_8_out);
  nand nand_10 (nand_10_out, nand_1_out, dflipflop_3_q);
  nand nand_11 (nand_11_out, nand_7_out, nand_10_out);
  _2_1MUX u_2_1mux_3 (.I0(dflipflop_2_q), .I1(nand_11_out), .S0(SHIFT), .Output(n2_1mux_3_output));
  _2_1MUX u_2_1mux_4 (
    .I0(n2_1mux_3_output), .I1(P2), .S0(INPUT_MODE_1_ParallelIn__0_SerialIn), .Output(n2_1mux_4_output));
  nand nand_12 (nand_12_out, dflipflop_2_q, DIR_1______0);
  nand nand_13 (nand_13_out, nand_12_out, nand_16_out);
  DFlipFlop dflipflop_2 (
    .D(n2_1mux_4_output), .Clk(Clk), .Q(dflipflop_2_q), .PRE_prime(PRE_prime), .CLR_prime(CLR_prime));  // open: Q_prime
  nand nand_14 (nand_14_out, OUTPUT_MODE_Parallel_1__Serial_0, dflipflop_2_q);
  nand nand_15 (O2, nand_14_out, nand_14_out);
  nand nand_16 (nand_16_out, nand_1_out, dflipflop_4_q);
  _2_1MUX u_2_1mux_5 (.I0(dflipflop_3_q), .I1(nand_13_out), .S0(SHIFT), .Output(n2_1mux_5_output));
  _2_1MUX u_2_1mux_6 (.I0(n2_1mux_5_output), .I1(P1), .S0(INPUT_MODE_1_ParallelIn__0_SerialIn));  // open: Output
  nand nand_17 (nand_17_out, OUTPUT_MODE_Parallel_1__Serial_0, dflipflop_3_q);
  nand nand_18 (O1, nand_17_out, nand_17_out);
  nand nand_19 (nand_19_out, dflipflop_3_q, DIR_1______0);
  nand nand_20 (nand_20_out, nand_19_out, nand_21_out);
  DFlipFlop dflipflop_3 (
    .Clk(Clk), .Q(dflipflop_3_q), .PRE_prime(PRE_prime), .CLR_prime(CLR_prime));  // open: D, Q_prime
  nand nand_21 (nand_21_out, nand_1_out, Rin);
  _2_1MUX u_2_1mux_7 (.I0(dflipflop_4_q), .I1(nand_20_out), .S0(SHIFT), .Output(n2_1mux_7_output));
  _2_1MUX u_2_1mux_8 (
    .I0(n2_1mux_7_output), .I1(P0), .S0(INPUT_MODE_1_ParallelIn__0_SerialIn), .Output(n2_1mux_8_output));
  DFlipFlop dflipflop_4 (
    .D(n2_1mux_8_output), .Clk(Clk), .Q(dflipflop_4_q), .PRE_prime(PRE_prime), .CLR_prime(CLR_prime));  // open: Q_prime
  nand nand_22 (nand_22_out, OUTPUT_MODE_Parallel_1__Serial_0, dflipflop_4_q);
  nand nand_23 (O0, nand_22_out, nand_22_out);
  nand nand_24 (nand_24_out, OUTPUT_MODE_Parallel_1__Serial_0, OUTPUT_MODE_Parallel_1__Serial_0);
  nand nand_25 (nand_25_out, dflipflop_4_q, nand_24_out);
  nand nand_26 (Rout, nand_25_out, nand_25_out);
endmodule

module _4bitRippleCounter (
  input  LOGIC1,
  input  PRE_prime,
  input  Clk,
  input  CLR_prime,
  output O,
  output O_2,
  output O_3,
  output O_4
);

  wire tflipflop_1_q_prime, tflipflop_2_q_prime, tflipflop_3_q_prime;

  TFlipFlop tflipflop_1 (
    .T(LOGIC1), .Clk(Clk), .Q(O), .Q_prime(tflipflop_1_q_prime), .PRE_prime(PRE_prime), .CLR_prime(CLR_prime));
  TFlipFlop tflipflop_2 (
    .T(LOGIC1), .Clk(tflipflop_1_q_prime), .Q(O_2), .Q_prime(tflipflop_2_q_prime), .PRE_prime(PRE_prime),
    .CLR_prime(CLR_prime));
  TFlipFlop tflipflop_3 (
    .T(LOGIC1), .Clk(tflipflop_2_q_prime), .Q(O_3), .Q_prime(tflipflop_3_q_prime), .PRE_prime(PRE_prime),
    .CLR_prime(CLR_prime));
  TFlipFlop tflipflop_4 (
    .T(LOGIC1), .Clk(tflipflop_3_q_prime), .Q(O_4), .PRE_prime(PRE_prime), .CLR_prime(CLR_prime));  // open: Q_prime
endmodule
